// Logisim project BREADBOARD_COMPUTER.circ as structural Verilog: 22 circuits, main circuit BRB_COMPUTER
module main (
);

  wire and_1_out, and_2_out, and_3_out, and_4_out, and_5_out, and_6_out, and_7_out, and_8_out, and_9_out,
       and_10_out, and_11_out, and_12_out, and_13_out, BUTTONS, clk_out, clock_1_out, comparator_1_eq,
       CPU_SOFTWARE_INT, edge_detector2_1_q, KB, minimal_cpu_1_inst_req, minimal_cpu_1_int,
       minimal_cpu_1_mem_r, minimal_cpu_1_mem_w, mmu_1_clk_out, mmu_1_d_grant, mmu_1_inst_grant,
       mmu_1_rom_grant, nand_1_out, not_1_out, not_2_out, or_1_out, or_2_out, or_3_out, pull_resistor_1_node,
       R, r_a, reg_file_1_e0, reg_file_1_e3, reg_file_1_e4, reg_file_1_e5, reg_file_1_e6, reg_file_1_e7,
       reg_file_2_e0, reg_file_2_e1, reg_file_2_e2, reg_file_2_e3, reg_file_2_e4, reg_file_2_e5,
       reg_file_2_e6, reg_file_2_e7, RESET_out, ROM_ACTIVE, ROM_APPROVED, rom_cpu_1_rom_req, ROM_DONE,
       ROM_OFF_WE, ROM_START_WE, s_r_l_1_q, SLEEP_out, smal_and_1_q, smal_and_2_q, smal_and_3_q,
       smal_and_4_q, smal_and_5_q, smal_and_6_q, smal_and_7_q, smal_and_8_q, smal_and_9_q, smal_and_10_q,
       smal_and_11_q, smal_and_12_q, smal_and_13_q, smal_and_14_q, smal_and_15_q, t_ff_1_q, undriven,
       undriven_2, undriven_3, undriven_4, undriven_5, undriven_6, undriven_7, undriven_8, undriven_9,
       undriven_10, undriven_11, undriven_12, W;
  wire [4:0] joystick_1_x, joystick_1_y;
  wire [5:0] button_1_out;
  wire [6:0] keyboard_1_data, reg_file_1_q0;
  wire [14:11] pull_resistor_5_node;
  wire [15:0] ADDR, BIOS_data, controlled_buffer_2_out, controlled_buffer_4_out, minimal_cpu_1_d_q,
       minimal_cpu_1_inst_addr, minimal_cpu_1_status, reg_file_1_q1, reg_file_1_q2, reg_file_1_q3,
       reg_file_1_q4, reg_file_1_q5, reg_file_1_q6, reg_file_1_q7, reg_file_2_q0, reg_file_2_q1,
       reg_file_2_q2, reg_file_2_q3, reg_file_2_q4, reg_file_2_q5, reg_file_2_q6, reg_file_2_q7, RET_ADDR_q,
       rom_1_data, rom_cpu_1_address, STAT_REG_q;
  wire [15:7] reg_file_1_q0_2;

  and and_1 (and_1_out, W, ROM_START_WE);
  and and_2 (and_2_out, W, ROM_OFF_WE);
  Pull_Resistor pull_resistor_1 (.node(pull_resistor_1_node));
  buf buffer_1 (pull_resistor_1_node, ROM_DONE);
  buf buffer_2 (pull_resistor_1_node, KB);
  buf buffer_3 (pull_resistor_1_node, BUTTONS);
  buf buffer_4 (pull_resistor_1_node, undriven);
  buf buffer_5 (pull_resistor_1_node, undriven_2);
  buf buffer_6 (pull_resistor_1_node, undriven_3);
  buf buffer_7 (pull_resistor_1_node, undriven_4);
  buf buffer_8 (pull_resistor_1_node, undriven_5);
  buf buffer_9 (pull_resistor_1_node, undriven_6);
  buf buffer_10 (pull_resistor_1_node, undriven_7);
  buf buffer_11 (pull_resistor_1_node, undriven_8);
  buf buffer_12 (pull_resistor_1_node, undriven_9);
  buf buffer_13 (pull_resistor_1_node, undriven_10);
  buf buffer_14 (pull_resistor_1_node, undriven_11);
  buf buffer_15 (pull_resistor_1_node, undriven_12);
  buf buffer_16 (pull_resistor_1_node, CPU_SOFTWARE_INT);
  ROM_CPU rom_cpu_1 (
    .START_WE(and_1_out), .TRANSFER_GRANT(mmu_1_rom_grant), .ADDR(controlled_buffer_2_out),
    .FINISH_WE(and_2_out), .CLK(mmu_1_clk_out), .WE_CLK(or_3_out), .DONE_ACCEPTED(ROM_APPROVED),
    .ADDRESS(rom_cpu_1_address), .DONE(ROM_DONE), .ROM_REQ(rom_cpu_1_rom_req), .active(r_a));
  not not_1 (not_1_out, or_3_out);
  or or_1 (or_1_out, minimal_cpu_1_mem_w, minimal_cpu_1_mem_r);
  edge_detector2 edge_detector2_1 (.HIGH(1'b0), .LOW(1'b1), .CLK(or_3_out), .Q(edge_detector2_1_q));
  S_R_L s_r_l_1 (.SET(RESET_out), .RESET(edge_detector2_1_q), .POR_RES(1'b0), .Q(s_r_l_1_q));
  Button RESET (.out(RESET_out));
  assign ADDR = mmu_1_rom_grant ? rom_cpu_1_address : 16'bz;  // Controlled_Buffer controlled_buffer_1
  Button SLEEP (.out(SLEEP_out));
  T_Flip_Flop t_ff_1 (.T(SLEEP_out), .clk(SLEEP_out), .Q(t_ff_1_q));  // open: Qn, reset, preset
  ROM #(.addrWidth(16), .dataWidth(16)) rom_1 (.addr(rom_cpu_1_address), .data(rom_1_data));
  MMU mmu_1 (
    .CPU_CLK(or_3_out), .ROM_CLK(or_3_out), .INST_CLK(not_1_out), .D_REQ(or_1_out),
    .ROM_REQ(rom_cpu_1_rom_req), .INST_REQ(minimal_cpu_1_inst_req), .res(s_r_l_1_q), .CLK_OUT(mmu_1_clk_out),
    .D_GRANT(mmu_1_d_grant), .ROM_GRANT(mmu_1_rom_grant), .INST_GRANT(mmu_1_inst_grant));
  assign controlled_buffer_2_out = mmu_1_rom_grant ? rom_1_data : 16'bz;  // Controlled_Buffer controlled_buffer_2
  and and_3 (and_3_out, minimal_cpu_1_mem_r, mmu_1_d_grant);
  and and_4 (and_4_out, minimal_cpu_1_mem_w, mmu_1_d_grant);
  Pull_Resistor pull_resistor_2 (.node(ADDR));
  Pull_Resistor pull_resistor_3 (.node(controlled_buffer_2_out));
  // Probe on controlled_buffer_2_out
  assign controlled_buffer_2_out = and_4_out ? minimal_cpu_1_d_q : 16'bz;  // Controlled_Buffer controlled_buffer_3
  assign controlled_buffer_4_out = and_3_out ? controlled_buffer_2_out : 16'bz;  // Controlled_Buffer controlled_buffer_4
  MEM_ARBITER mem_arbiter_1 (
    .INST_GRANT(mmu_1_inst_grant), .D_GRANT(mmu_1_d_grant), .ROM_GRANT(mmu_1_rom_grant),
    .CPU_R(minimal_cpu_1_mem_r), .CPU_W(minimal_cpu_1_mem_w), .MEM_R(R), .MEM_W(W));
  minimal_cpu minimal_cpu_1 (
    .RESET(s_r_l_1_q), .D_IN(controlled_buffer_4_out), .HALT(t_ff_1_q), .DATA_GRANT(mmu_1_d_grant),
    .INST_G(mmu_1_inst_grant), .INST(controlled_buffer_2_out), .CLK(or_3_out), .IRQ(pull_resistor_1_node),
    .INT(minimal_cpu_1_int), .INST_ADDR(minimal_cpu_1_inst_addr), .STATUS(minimal_cpu_1_status),
    .D_Q(minimal_cpu_1_d_q), .ADDR(ADDR), .SOFT_INT(CPU_SOFTWARE_INT), .MEM_W(minimal_cpu_1_mem_w),
    .MEM_R(minimal_cpu_1_mem_r), .INST_REQ(minimal_cpu_1_inst_req));
  and and_5 (and_5_out, ADDR[9], ADDR[10], ~ADDR[11]);  // AND_Gate
  and and_6 (and_6_out, ADDR[12], ADDR[13], ADDR[14], ADDR[15], 1'b1);
  Register #(.width(16)) RET_ADDR (
    .D(minimal_cpu_1_inst_addr), .en(minimal_cpu_1_int), .clk(minimal_cpu_1_int), .Q(RET_ADDR_q),
    .clr(s_r_l_1_q));
  Register #(.width(16)) STAT_REG (
    .D(minimal_cpu_1_status), .en(minimal_cpu_1_int), .clk(minimal_cpu_1_int), .Q(STAT_REG_q), .clr(s_r_l_1_q));
  or or_2 (or_2_out, and_5_out, ADDR[11]);
  nand nand_1 (nand_1_out, or_2_out, and_6_out);
  Comparator #(.mode("unsigned"), .width(16)) comparator_1 (
    .a(minimal_cpu_1_inst_addr), .eq(comparator_1_eq));  // open: b, gt, lt
  and and_7 (and_7_out, ~ADDR[8], and_6_out, and_5_out);  // AND_Gate
  and and_8 (and_8_out, ADDR[11], and_6_out);
  Clock clock_1 (.out(clock_1_out));
  Pull_Resistor pull_resistor_4 (.node(comparator_1_eq));
  and and_9 (and_9_out, ~comparator_1_eq, clock_1_out);  // AND_Gate
  Button clk (.out(clk_out));
  or or_3 (or_3_out, and_9_out, clk_out);
  and and_10 (and_10_out, and_7_out, ADDR[4], ADDR[5], ADDR[6], ADDR[7]);
  ROM #(.dataWidth(16)) BIOS (.addr(ADDR[7:0]), .data(BIOS_data));
  RAM #(.addrWidth(16), .asyncread("true"), .dataWidth(16), .databus("bidir")) ram_1 (
    .addr(ADDR), .we(and_11_out), .oe(and_12_out), .clk(mmu_1_clk_out), .data(controlled_buffer_2_out));
  and and_11 (and_11_out, nand_1_out, W);
  and and_12 (and_12_out, nand_1_out, R);
  // RGB_Video #(.cursor("No Cursor"), .height(32), .scale(6), .width(64)) rgb_video_1: pin names not known; wires that end beside it: s_r_l_1_q, mmu_1_clk_out, and_8_out, controlled_buffer_2_out, controlled_buffer_2_out
  Keyboard keyboard_1 (.clk(mmu_1_clk_out), .re(smal_and_4_q), .clr(s_r_l_1_q), .avail(KB), .data(keyboard_1_data));
  assign controlled_buffer_2_out = and_13_out ? BIOS_data : 16'bz;  // Controlled_Buffer controlled_buffer_5
  and and_13 (and_13_out, ~ADDR[11], ADDR[10], ADDR[9], ADDR[8], R);  // AND_Gate
  Joystick #(.bits(5)) joystick_1 (.x(joystick_1_x), .y(joystick_1_y));
  Button button_1 (.out(button_1_out[0]));
  Button button_2 (.out(button_1_out[3]));
  Button button_3 (.out(button_1_out[1]));
  Button button_4 (.out(button_1_out[2]));
  Button ENT (.out(button_1_out[4]));
  Button DEL (.out(button_1_out[5]));
  Pull_Resistor pull_resistor_5 (.node({CPU_SOFTWARE_INT, pull_resistor_5_node, ROM_ACTIVE, ROM_DONE, BUTTONS, KB, keyboard_1_data}));
  TTY tty_1 (.data(reg_file_1_q0), .clk(mmu_1_clk_out), .we(reg_file_1_e0), .clr(reg_file_1_q0_2[7]));
  not not_2 (not_2_out, and_10_out);
  reg_file reg_file_1 (
    .NE(ADDR[3]), .E(and_10_out), .SEL(ADDR[2:0]), .D0(controlled_buffer_2_out),
    .D1(controlled_buffer_2_out), .D2(controlled_buffer_2_out),
    .D3({joystick_1_y, joystick_1_x, button_1_out}),
    .D4({CPU_SOFTWARE_INT, pull_resistor_5_node, ROM_ACTIVE, ROM_DONE, BUTTONS, KB, keyboard_1_data}),
    .D5(RET_ADDR_q), .D6(STAT_REG_q), .D7(controlled_buffer_2_out), .CLK(mmu_1_clk_out), .RES(s_r_l_1_q),
    .Q0({reg_file_1_q0_2[15:9], ROM_APPROVED, reg_file_1_q0_2[7], reg_file_1_q0}), .Q1(reg_file_1_q1),
    .Q2(reg_file_1_q2), .Q3(reg_file_1_q3), .Q4(reg_file_1_q4), .Q5(reg_file_1_q5), .Q6(reg_file_1_q6),
    .Q7(reg_file_1_q7), .E0(reg_file_1_e0), .E1(ROM_START_WE), .E2(ROM_OFF_WE), .E3(reg_file_1_e3),
    .E4(reg_file_1_e4), .E5(reg_file_1_e5), .E6(reg_file_1_e6), .E7(reg_file_1_e7));
  SMAL_AND smal_and_1 (.A(ROM_START_WE), .B(R), .Q(smal_and_1_q));
  SMAL_AND smal_and_2 (.A(ROM_OFF_WE), .B(R), .Q(smal_and_2_q));
  SMAL_AND smal_and_3 (.A(reg_file_1_e3), .B(R), .Q(smal_and_3_q));
  SMAL_AND smal_and_4 (.A(reg_file_1_e4), .B(R), .Q(smal_and_4_q));
  SMAL_AND smal_and_5 (.A(reg_file_1_e5), .B(R), .Q(smal_and_5_q));
  SMAL_AND smal_and_6 (.A(reg_file_1_e6), .B(R), .Q(smal_and_6_q));
  SMAL_AND smal_and_7 (.A(reg_file_1_e7), .B(R), .Q(smal_and_7_q));
  reg_file reg_file_2 (
    .NE(not_2_out), .E(ADDR[3]), .SEL(ADDR[2:0]), .D0(controlled_buffer_2_out), .D1(controlled_buffer_2_out),
    .D2(controlled_buffer_2_out), .D3(controlled_buffer_2_out), .D4(controlled_buffer_2_out),
    .D5(controlled_buffer_2_out), .D6(controlled_buffer_2_out), .D7(controlled_buffer_2_out),
    .CLK(mmu_1_clk_out), .RES(s_r_l_1_q), .Q0(reg_file_2_q0), .Q1(reg_file_2_q1), .Q2(reg_file_2_q2),
    .Q3(reg_file_2_q3), .Q4(reg_file_2_q4), .Q5(reg_file_2_q5), .Q6(reg_file_2_q6), .Q7(reg_file_2_q7),
    .E0(reg_file_2_e0), .E1(reg_file_2_e1), .E2(reg_file_2_e2), .E3(reg_file_2_e3), .E4(reg_file_2_e4),
    .E5(reg_file_2_e5), .E6(reg_file_2_e6), .E7(reg_file_2_e7));
  SMAL_AND smal_and_8 (.A(reg_file_2_e0), .B(R), .Q(smal_and_8_q));
  SMAL_AND smal_and_9 (.A(reg_file_2_e1), .B(R), .Q(smal_and_9_q));
  SMAL_AND smal_and_10 (.A(reg_file_2_e2), .B(R), .Q(smal_and_10_q));
  SMAL_AND smal_and_11 (.A(reg_file_2_e3), .B(R), .Q(smal_and_11_q));
  SMAL_AND smal_and_12 (.A(reg_file_2_e4), .B(R), .Q(smal_and_12_q));
  SMAL_AND smal_and_13 (.A(reg_file_2_e5), .B(R), .Q(smal_and_13_q));
  SMAL_AND smal_and_14 (.A(reg_file_2_e6), .B(R), .Q(smal_and_14_q));
  SMAL_AND smal_and_15 (.A(reg_file_2_e7), .Q(smal_and_15_q));  // open: B
  or or_4 (BUTTONS, 1'b0, reg_file_1_q3[0], reg_file_1_q3[1], reg_file_1_q3[2], reg_file_1_q3[3], reg_file_1_q3[4], reg_file_1_q3[5]);
  assign controlled_buffer_2_out = smal_and_1_q ? reg_file_1_q1 : 16'bz;  // Controlled_Buffer controlled_buffer_6
  assign controlled_buffer_2_out = smal_and_2_q ? reg_file_1_q2 : 16'bz;  // Controlled_Buffer controlled_buffer_7
  assign controlled_buffer_2_out = smal_and_3_q ? reg_file_1_q3 : 16'bz;  // Controlled_Buffer controlled_buffer_8
  assign controlled_buffer_2_out = smal_and_4_q ? reg_file_1_q4 : 16'bz;  // Controlled_Buffer controlled_buffer_9
  assign controlled_buffer_2_out = smal_and_5_q ? reg_file_1_q5 : 16'bz;  // Controlled_Buffer controlled_buffer_10
  assign controlled_buffer_2_out = smal_and_6_q ? reg_file_1_q6 : 16'bz;  // Controlled_Buffer controlled_buffer_11
  assign controlled_buffer_2_out = smal_and_7_q ? reg_file_1_q7 : 16'bz;  // Controlled_Buffer controlled_buffer_12
  assign controlled_buffer_2_out = smal_and_8_q ? reg_file_2_q0 : 16'bz;  // Controlled_Buffer controlled_buffer_13
  assign controlled_buffer_2_out = smal_and_9_q ? reg_file_2_q1 : 16'bz;  // Controlled_Buffer controlled_buffer_14
  assign controlled_buffer_2_out = smal_and_10_q ? reg_file_2_q2 : 16'bz;  // Controlled_Buffer controlled_buffer_15
  assign controlled_buffer_2_out = smal_and_11_q ? reg_file_2_q3 : 16'bz;  // Controlled_Buffer controlled_buffer_16
  assign controlled_buffer_2_out = smal_and_12_q ? reg_file_2_q4 : 16'bz;  // Controlled_Buffer controlled_buffer_17
  assign controlled_buffer_2_out = smal_and_13_q ? reg_file_2_q5 : 16'bz;  // Controlled_Buffer controlled_buffer_18
  assign controlled_buffer_2_out = smal_and_14_q ? reg_file_2_q6 : 16'bz;  // Controlled_Buffer controlled_buffer_19
  assign controlled_buffer_2_out = smal_and_15_q ? reg_file_2_q7 : 16'bz;  // Controlled_Buffer controlled_buffer_20

  // Notes on the sheet:
  //   buffer_1 drives only 1 and floats otherwise
  //   buffer_2 drives only 1 and floats otherwise
  //   buffer_3 drives only 1 and floats otherwise
  //   buffer_4 drives only 1 and floats otherwise
  //   buffer_5 drives only 1 and floats otherwise
  //   buffer_6 drives only 1 and floats otherwise
  //   buffer_7 drives only 1 and floats otherwise
  //   buffer_8 drives only 1 and floats otherwise
  //   buffer_9 drives only 1 and floats otherwise
  //   buffer_10 drives only 1 and floats otherwise
  //   buffer_11 drives only 1 and floats otherwise
  //   buffer_12 drives only 1 and floats otherwise
  //   buffer_13 drives only 1 and floats otherwise
  //   buffer_14 drives only 1 and floats otherwise
  //   buffer_15 drives only 1 and floats otherwise
  //   buffer_16 drives only 1 and floats otherwise
  //   contents of BIOS (hex, n*v repeats v):
  //   0 d003 f7bd 1003 1 dd01 c d054 f770 f003 ff 3 f6f3 1007 20 1006 f71c f603 1 9 f70c f603 80 3 f6f0 b
  //   f72a f003 80 3 f6f0 b f7e8 1003 1 dd01 c d054 f770 f003 f750 f003 f5ff 3 f6f2 b 0 3 f6f1 b 0 1003 0
  //   2003 0 3003 0 4003 0 5003 0 6003 0 7003 0 8003 0 9003 0 a003 0 b003 0 c003 10 e003 0 d003 0 13 f7f9
  //   1003 1 dd01 c d054 f788 f003 20 e006 f75e f603 f750 f003 0 13 16*0 1 dd01 2 d054 f778 f003 f6f0 200b
  //   20 1050 1 1101 0 2002 f776 f603 20 d050 1 dd09 f0 d050 1 dd09 f6f3 4007 10 4006 f788 f103 f6f4 2007
  //   80 2006 f7aa f103 7f 2215 f6f0 200b 30 1050 1 1101 0 3002 f7a6 f103 2 3028 f7aa f603 f78e f003 20
  //   ee11 f7ac f003 ffdf ee15 f0 d050 1 dd09 13*0 42 6f 6f 74 69 6e 67 2e 2e 2e a 70 72 65 73 73 20 64 65
  //   6c 20 74 6f 20 65 6e 74 65 72 20 63 6d 64 20 70 72 6f 6d 70 74 0 0 0 63 6f 6d 6d 61 6e 64 20 70 72
  //   6f 6d 70 74 3a a 0 65 78 69 74 0 0 1000
  //   F700-F7FF
  //   0000 - F5FF
  //   F800-FFFF
  //   F5FF - FFFF
  //   |
  //   V
  //   F6F0 - F6FF
endmodule

module reg_file (
  input  [15:0] D0,
  input  [15:0] D1,
  input  [15:0] D2,
  input  [15:0] D3,
  input  NE,
  input  E,
  input  [2:0] SEL,
  input  [15:0] D4,
  input  [15:0] D5,
  input  [15:0] D6,
  input  [15:0] D7,
  input  CLK,
  input  RES,
  output [15:0] Q0,
  output E0,
  output [15:0] Q1,
  output E1,
  output [15:0] Q2,
  output E2,
  output [15:0] Q3,
  output E3,
  output [15:0] Q4,
  output E4,
  output [15:0] Q5,
  output E5,
  output [15:0] Q6,
  output E6,
  output [15:0] Q7,
  output E7
);

  wire and_1_out;

  Decoder #(.select(3)) decoder_1 (
    .out0(E0), .out1(E1), .out2(E2), .out3(E3), .out4(E4), .out5(E5), .out6(E6), .out7(E7), .sel(SEL),
    .en(and_1_out));
  and and_1 (and_1_out, ~NE, E);  // AND_Gate
  Register #(.trigger("falling"), .width(16)) register_1 (.D(D0), .en(E0), .clk(CLK), .Q(Q0), .clr(RES));
  Register #(.trigger("falling"), .width(16)) register_2 (.D(D1), .en(E1), .clk(CLK), .Q(Q1), .clr(RES));
  Register #(.trigger("falling"), .width(16)) register_3 (.D(D2), .en(E2), .clk(CLK), .Q(Q2), .clr(RES));
  Register #(.trigger("falling"), .width(16)) register_4 (.D(D3), .en(E3), .clk(CLK), .Q(Q3), .clr(RES));
  Register #(.trigger("falling"), .width(16)) register_5 (.D(D4), .en(E4), .clk(CLK), .Q(Q4), .clr(RES));
  Register #(.trigger("falling"), .width(16)) register_6 (.D(D5), .en(E5), .clk(CLK), .Q(Q5), .clr(RES));
  Register #(.trigger("falling"), .width(16)) register_7 (.D(D6), .en(E6), .clk(CLK), .Q(Q6), .clr(RES));
  Register #(.trigger("falling"), .width(16)) register_8 (.D(D7), .en(E7), .clk(CLK), .Q(Q7), .clr(RES));
endmodule

module PC (
  input  W,
  input  [15:0] data,
  input  clk,
  input  INC,
  output [15:0] Q
);

  wire buffer_1_out, buffer_2_out, buffer_3_out, buffer_4_out, buffer_5_out, buffer_6_out, buffer_7_out,
       buffer_8_out, buffer_9_out;

  Pull_Resistor pull_resistor_1 (.node(Q[0]));
  Counter #(.max('h7fff), .width(15)) pc_c (
    .load(W), .D(data[15:1]), .count(INC), .Q(Q[15:1]), .up(1'b1), .clk(clk), .clr(1'b0));  // open: carry
  buf buffer_1 (buffer_1_out, clk);
  buf buffer_2 (buffer_2_out, buffer_1_out);
  buf buffer_3 (buffer_3_out, buffer_2_out);
  buf buffer_4 (buffer_4_out, buffer_3_out);
  buf buffer_5 (buffer_5_out, buffer_4_out);
  buf buffer_6 (buffer_6_out, buffer_5_out);
  Register #(.width(16)) register_1 (.D(Q), .en(buffer_7_out), .clk(buffer_8_out), .clr(1'b0));  // open: Q
  buf buffer_7 (buffer_7_out, buffer_9_out);
  buf buffer_8 (buffer_8_out, buffer_7_out);
  buf buffer_9 (buffer_9_out, buffer_6_out);
endmodule

module STATUS_REG (
  input  BUS_SEL,
  input  [3:0] ALU_F,
  input  [7:0] BUS_DATA,
  input  F_W,
  input  CLK,
  input  RES,
  output [7:0] BUS_Q,
  output [3:0] F_Q
);

  wire [7:0] bit_extender_1_out, multiplexer_1_out;

  assign bit_extender_1_out = {{4{1'b0}}, ALU_F};  // Bit_Extender bit_extender_1
  Register register_1 (.D(multiplexer_1_out), .en(F_W), .clk(CLK), .Q(BUS_Q), .clr(RES));
  Multiplexer #(.width(8)) multiplexer_1 (
    .in0(bit_extender_1_out), .in1(BUS_DATA), .out(multiplexer_1_out), .sel(BUS_SEL));

  assign F_Q = BUS_Q[3:0];
endmodule

module ALU (
  input  c_in,
  input  [15:0] b,
  input  [15:0] a,
  input  [3:0] M_OP,
  output [15:0] Q,
  output [3:0] FLAGS
);

  wire adder_1_cout, multiplexer_3_out, xor_1_out, xor_2_out;
  wire [1:0] c_op, sh_op;
  wire [2:0] rom_1_data;
  wire [15:0] b_t, multiplexer_2_out;
  wire [15:15] multiplexer_1_out;

  ROM #(.addrWidth(4), .dataWidth(7)) rom_1 (.addr(M_OP), .data({c_op, sh_op, rom_1_data}));
  ROM #(.addrWidth(19)) rom_2 (.addr({rom_1_data, b[15:8], a[15:8]}), .data(b_t[15:8]));
  ROM #(.addrWidth(19)) rom_3 (.addr({rom_1_data, b[7:0], a[7:0]}), .data(b_t[7:0]));
  Multiplexer #(.select(2)) multiplexer_1 (
    .in0(c_in), .in1(1'b0), .in2(1'b1), .in3(a[15]), .out(multiplexer_1_out[15]));  // open: sel
  Multiplexer #(.select(2), .width(16)) multiplexer_2 (
    .in0({16{1'b0}}), .in1({multiplexer_1_out[15], a[15:1]}), .in2({a[14:0], multiplexer_1_out[15]}),
    .in3(a), .out(multiplexer_2_out), .sel(sh_op));
  Multiplexer #(.select(2)) multiplexer_3 (
    .in0(multiplexer_1_out[15]), .in1(1'b0), .in2(1'b0), .in3(multiplexer_1_out[15]), .out(multiplexer_3_out));  // open: sel
  Multiplexer #(.select(2)) multiplexer_4 (
    .in0(adder_1_cout), .in1(a[0]), .in2(a[15]), .in3(adder_1_cout), .out(FLAGS[2]));  // open: sel
  Adder #(.width(16)) adder_1 (
    .a(multiplexer_2_out), .b(b_t), .out({FLAGS[1], Q[14:0]}), .cin(multiplexer_3_out), .cout(adder_1_cout));
  nor nor_1 (FLAGS[0], FLAGS[1], Q[14], Q[13], Q[12], Q[11], Q[10], Q[9], Q[8], Q[7], Q[6], Q[5], Q[4], Q[3], Q[2], Q[1], Q[0], 1'b0);
  xor xor_1 (xor_1_out, a[15], FLAGS[1]);
  and and_1 (FLAGS[3], xor_1_out, xor_2_out);
  xor xor_2 (xor_2_out, FLAGS[1], b_t[15]);

  assign Q[15] = FLAGS[1];

  // Notes on the sheet:
  //   contents of rom_1 (hex, n*v repeats v):
  //   38 18 59 19 21 41 22 23 24 28 8 30 10 68 20
  //   contents of rom_2 (hex, n*v repeats v):
  //   256*0 256*1 256*2 256*3 256*4 256*5 256*6 256*7 256*8 256*9 256*a 256*b 256*c 256*d 256*e 256*f
  //   256*10 256*11 256*12 256*13 256*14 256*15 256*16 256*17 256*18 256*19 256*1a 256*1b 256*1c 256*1d
  //   256*1e 256*1f 256*20 256*21 256*22 256*23 256*24 256*25 256*26 256*27 256*28 256*29 256*2a 256*2b
  //   256*2c 256*2d 256*2e 256*2f 256*30 256*31 256*32 256*33 256*34 256*35 256*36 256*37 256*38 256*39
  //   256*3a 256*3b 256*3c 256*3d 256*3e 256*3f 256*40 256*41 256*42 256*43 256*44 256*45 256*46 256*47
  //   256*48 256*49 256*4a 256*4b 256*4c 256*4d 256*4e 256*4f 256*50 256*51 256*52 256*53 256*54 256*55
  //   256*56 256*57 256*58 256*59 256*5a 256*5b 256*5c 256*5d 256*5e 256*5f 256*60 256*61 256*62 256*63
  //   256*64 256*65 256*66 256*67 256*68 256*69 256*6a 256*6b 256*6c 256*6d 256*6e 256*6f 256*70 256*71
  //   256*72 256*73 256*74 256*75 256*76 256*77 256*78 256*79 256*7a 256*7b 256*7c 256*7d 256*7e 256*7f
  //   256*80 256*81 256*82 256*83 256*84 256*85 256*86 256*87 256*88 256*89 256*8a 256*8b 256*8c 256*8d
  //   256*8e 256*8f 256*90 256*91 256*92 256*93 256*94 256*95 256*96 256*97 256*98 256*99 256*9a 256*9b
  //   256*9c 256*9d 256*9e 256*9f 256*a0 256*a1 256*a2 256*a3 256*a4 256*a5 256*a6 256*a7 256*a8 256*a9
  //   256*aa 256*ab 256*ac 256*ad 256*ae 256*af 256*b0 256*b1 256*b2 256*b3 256*b4 256*b5 256*b6 256*b7
  //   256*b8 256*b9 256*ba 256*bb 256*bc 256*bd 256*be 256*bf 256*c0 256*c1 256*c2 256*c3 256*c4 256*c5
  //   256*c6 256*c7 256*c8 256*c9 256*ca 256*cb 256*cc 256*cd 256*ce 256*cf 256*d0 256*d1 256*d2 256*d3
  //   256*d4 256*d5 256*d6 256*d7 256*d8 256*d9 256*da 256*db 256*dc 256*dd 256*de 256*df 256*e0 256*e1
  //   256*e2 256*e3 256*e4 256*e5 256*e6 256*e7 256*e8 256*e9 256*ea 256*eb 256*ec 256*ed 256*ee 256*ef
  //   256*f0 256*f1 256*f2 256*f3 256*f4 256*f5 256*f6 256*f7 256*f8 256*f9 256*fa 256*fb 256*fc 256*fd
  //   256*fe 512*ff 256*fe 256*fd 256*fc 256*fb 256*fa 256*f9 256*f8 256*f7 256*f6 256*f5 256*f4 256*f3
  //   256*f2 256*f1 256*f0 256*ef 256*ee 256*ed 256*ec 256*eb 256*ea 256*e9 256*e8 256*e7 256*e6 256*e5
  //   256*e4 256*e3 256*e2 256*e1 256*e0 256*df 256*de 256*dd 256*dc 256*db 256*da 256*d9 256*d8 256*d7
  //   256*d6 256*d5 256*d4 256*d3 256*d2 256*d1 256*d0 256*cf 256*ce 256*cd 256*cc 256*cb 256*ca 256*c9
  //   256*c8 256*c7 256*c6 256*c5 256*c4 256*c3 256*c2 256*c1 256*c0 256*bf 256*be 256*bd 256*bc 256*bb
  //   256*ba 256*b9 256*b8 256*b7 256*b6 256*b5 256*b4 256*b3 256*b2 256*b1 256*b0 256*af 256*ae 256*ad
  //   256*ac 256*ab 256*aa 256*a9 256*a8 256*a7 256*a6 256*a5 256*a4 256*a3 256*a2 256*a1 256*a0 256*9f
  //   256*9e 256*9d 256*9c 256*9b 256*9a 256*99 256*98 256*97 256*96 256*95 256*94 256*93 256*92 256*91
  //   256*90 256*8f 256*8e 256*8d 256*8c 256*8b 256*8a 256*89 256*88 256*87 256*86 256*85 256*84 256*83
  //   256*82 256*81 256*80 256*7f 256*7e 256*7d 256*7c 256*7b 256*7a 256*79 256*78 256*77 256*76 256*75
  //   256*74 256*73 256*72 256*71 256*70 256*6f 256*6e 256*6d 256*6c 256*6b 256*6a 256*69 256*68 256*67
  //   256*66 256*65 256*64 256*63 256*62 256*61 256*60 256*5f 256*5e 256*5d 256*5c 256*5b 256*5a 256*59
  //   256*58 256*57 256*56 256*55 256*54 256*53 256*52 256*51 256*50 256*4f 256*4e 256*4d 256*4c 256*4b
  //   256*4a 256*49 256*48 256*47 256*46 256*45 256*44 256*43 256*42 256*41 256*40 256*3f 256*3e 256*3d
  //   256*3c 256*3b 256*3a 256*39 256*38 256*37 256*36 256*35 256*34 256*33 256*32 256*31 256*30 256*2f
  //   256*2e 256*2d 256*2c 256*2b 256*2a 256*29 256*28 256*27 256*26 256*25 256*24 256*23 256*22 256*21
  //   256*20 256*1f 256*1e 256*1d 256*1c 256*1b 256*1a 256*19 256*18 256*17 256*16 256*15 256*14 256*13
  //   256*12 256*11 256*10 256*f 256*e 256*d 256*c 256*b 256*a 256*9 256*8 256*7 256*6 256*5 256*4 256*3
  //   256*2 256*1 257*0 1 2 3 4 5 6 7 8 9 a b c d e f 10 11 12 13 14 15 16 17 18 19 1a 1b 1c 1d 1e 1f 20
  //   21 22 23 24 25 26 27 28 29 2a 2b 2c 2d 2e 2f 30 31 32 33 34 35 36 37 38 39 3a 3b 3c 3d 3e 3f 40 41
  //   42 43 44 45 46 47 48 49 4a 4b 4c 4d 4e 4f 50 51 52 53 54 55 56 57 58 59 5a 5b 5c 5d 5e 5f 60 61 62
  //   63 64 65 66 67 68 69 6a 6b 6c 6d 6e 6f 70 71 72 73 74 75 76 77 78 79 7a 7b 7c 7d 7e 7f 80 81 82 83
  //   84 85 86 87 88 89 8a 8b 8c 8d 8e 8f 90 91 92 93 94 95 96 97 98 99 9a 9b 9c 9d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
  //   contents of rom_3 (hex, n*v repeats v):
  //   256*0 256*1 256*2 256*3 256*4 256*5 256*6 256*7 256*8 256*9 256*a 256*b 256*c 256*d 256*e 256*f
  //   256*10 256*11 256*12 256*13 256*14 256*15 256*16 256*17 256*18 256*19 256*1a 256*1b 256*1c 256*1d
  //   256*1e 256*1f 256*20 256*21 256*22 256*23 256*24 256*25 256*26 256*27 256*28 256*29 256*2a 256*2b
  //   256*2c 256*2d 256*2e 256*2f 256*30 256*31 256*32 256*33 256*34 256*35 256*36 256*37 256*38 256*39
  //   256*3a 256*3b 256*3c 256*3d 256*3e 256*3f 256*40 256*41 256*42 256*43 256*44 256*45 256*46 256*47
  //   256*48 256*49 256*4a 256*4b 256*4c 256*4d 256*4e 256*4f 256*50 256*51 256*52 256*53 256*54 256*55
  //   256*56 256*57 256*58 256*59 256*5a 256*5b 256*5c 256*5d 256*5e 256*5f 256*60 256*61 256*62 256*63
  //   256*64 256*65 256*66 256*67 256*68 256*69 256*6a 256*6b 256*6c 256*6d 256*6e 256*6f 256*70 256*71
  //   256*72 256*73 256*74 256*75 256*76 256*77 256*78 256*79 256*7a 256*7b 256*7c 256*7d 256*7e 256*7f
  //   256*80 256*81 256*82 256*83 256*84 256*85 256*86 256*87 256*88 256*89 256*8a 256*8b 256*8c 256*8d
  //   256*8e 256*8f 256*90 256*91 256*92 256*93 256*94 256*95 256*96 256*97 256*98 256*99 256*9a 256*9b
  //   256*9c 256*9d 256*9e 256*9f 256*a0 256*a1 256*a2 256*a3 256*a4 256*a5 256*a6 256*a7 256*a8 256*a9
  //   256*aa 256*ab 256*ac 256*ad 256*ae 256*af 256*b0 256*b1 256*b2 256*b3 256*b4 256*b5 256*b6 256*b7
  //   256*b8 256*b9 256*ba 256*bb 256*bc 256*bd 256*be 256*bf 256*c0 256*c1 256*c2 256*c3 256*c4 256*c5
  //   256*c6 256*c7 256*c8 256*c9 256*ca 256*cb 256*cc 256*cd 256*ce 256*cf 256*d0 256*d1 256*d2 256*d3
  //   256*d4 256*d5 256*d6 256*d7 256*d8 256*d9 256*da 256*db 256*dc 256*dd 256*de 256*df 256*e0 256*e1
  //   256*e2 256*e3 256*e4 256*e5 256*e6 256*e7 256*e8 256*e9 256*ea 256*eb 256*ec 256*ed 256*ee 256*ef
  //   256*f0 256*f1 256*f2 256*f3 256*f4 256*f5 256*f6 256*f7 256*f8 256*f9 256*fa 256*fb 256*fc 256*fd
  //   256*fe 512*ff 256*fe 256*fd 256*fc 256*fb 256*fa 256*f9 256*f8 256*f7 256*f6 256*f5 256*f4 256*f3
  //   256*f2 256*f1 256*f0 256*ef 256*ee 256*ed 256*ec 256*eb 256*ea 256*e9 256*e8 256*e7 256*e6 256*e5
  //   256*e4 256*e3 256*e2 256*e1 256*e0 256*df 256*de 256*dd 256*dc 256*db 256*da 256*d9 256*d8 256*d7
  //   256*d6 256*d5 256*d4 256*d3 256*d2 256*d1 256*d0 256*cf 256*ce 256*cd 256*cc 256*cb 256*ca 256*c9
  //   256*c8 256*c7 256*c6 256*c5 256*c4 256*c3 256*c2 256*c1 256*c0 256*bf 256*be 256*bd 256*bc 256*bb
  //   256*ba 256*b9 256*b8 256*b7 256*b6 256*b5 256*b4 256*b3 256*b2 256*b1 256*b0 256*af 256*ae 256*ad
  //   256*ac 256*ab 256*aa 256*a9 256*a8 256*a7 256*a6 256*a5 256*a4 256*a3 256*a2 256*a1 256*a0 256*9f
  //   256*9e 256*9d 256*9c 256*9b 256*9a 256*99 256*98 256*97 256*96 256*95 256*94 256*93 256*92 256*91
  //   256*90 256*8f 256*8e 256*8d 256*8c 256*8b 256*8a 256*89 256*88 256*87 256*86 256*85 256*84 256*83
  //   256*82 256*81 256*80 256*7f 256*7e 256*7d 256*7c 256*7b 256*7a 256*79 256*78 256*77 256*76 256*75
  //   256*74 256*73 256*72 256*71 256*70 256*6f 256*6e 256*6d 256*6c 256*6b 256*6a 256*69 256*68 256*67
  //   256*66 256*65 256*64 256*63 256*62 256*61 256*60 256*5f 256*5e 256*5d 256*5c 256*5b 256*5a 256*59
  //   256*58 256*57 256*56 256*55 256*54 256*53 256*52 256*51 256*50 256*4f 256*4e 256*4d 256*4c 256*4b
  //   256*4a 256*49 256*48 256*47 256*46 256*45 256*44 256*43 256*42 256*41 256*40 256*3f 256*3e 256*3d
  //   256*3c 256*3b 256*3a 256*39 256*38 256*37 256*36 256*35 256*34 256*33 256*32 256*31 256*30 256*2f
  //   256*2e 256*2d 256*2c 256*2b 256*2a 256*29 256*28 256*27 256*26 256*25 256*24 256*23 256*22 256*21
  //   256*20 256*1f 256*1e 256*1d 256*1c 256*1b 256*1a 256*19 256*18 256*17 256*16 256*15 256*14 256*13
  //   256*12 256*11 256*10 256*f 256*e 256*d 256*c 256*b 256*a 256*9 256*8 256*7 256*6 256*5 256*4 256*3
  //   256*2 256*1 257*0 1 2 3 4 5 6 7 8 9 a b c d e f 10 11 12 13 14 15 16 17 18 19 1a 1b 1c 1d 1e 1f 20
  //   21 22 23 24 25 26 27 28 29 2a 2b 2c 2d 2e 2f 30 31 32 33 34 35 36 37 38 39 3a 3b 3c 3d 3e 3f 40 41
  //   42 43 44 45 46 47 48 49 4a 4b 4c 4d 4e 4f 50 51 52 53 54 55 56 57 58 59 5a 5b 5c 5d 5e 5f 60 61 62
  //   63 64 65 66 67 68 69 6a 6b 6c 6d 6e 6f 70 71 72 73 74 75 76 77 78 79 7a 7b 7c 7d 7e 7f 80 81 82 83
  //   84 85 86 87 88 89 8a 8b 8c 8d 8e 8f 90 91 92 93 94 95 96 97 98 99 9a 9b 9c 9d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
endmodule

module reg_file2 (
  input  [15:0] DATA,
  input  [3:0] WA,
  input  BE,
  input  AE,
  input  WE,
  input  [3:0] BA,
  input  [3:0] AA,
  input  CLK,
  input  RES,
  input  [3:0] f_in,
  input  F_W,
  input  IRQ,
  output [15:0] B_Q,
  output [15:0] A_Q,
  output [15:0] f_q,
  output JMP,
  output [15:0] PC_D
);

  wire demultiplexer_1_out0, demultiplexer_1_out1, demultiplexer_1_out2, demultiplexer_1_out3,
       demultiplexer_1_out4, demultiplexer_1_out5, demultiplexer_1_out6, demultiplexer_1_out7,
       demultiplexer_1_out8, demultiplexer_1_out9, demultiplexer_1_out10, demultiplexer_1_out11,
       demultiplexer_1_out12, demultiplexer_1_out13, demultiplexer_1_out14, demultiplexer_1_out15,
       demultiplexer_2_out0, demultiplexer_2_out1, demultiplexer_2_out2, demultiplexer_2_out3,
       demultiplexer_2_out4, demultiplexer_2_out5, demultiplexer_2_out6, demultiplexer_2_out7,
       demultiplexer_2_out8, demultiplexer_2_out9, demultiplexer_2_out10, demultiplexer_2_out11,
       demultiplexer_2_out12, demultiplexer_2_out13, demultiplexer_2_out14, demultiplexer_2_out15,
       demultiplexer_3_out0, demultiplexer_3_out1, demultiplexer_3_out2, demultiplexer_3_out3,
       demultiplexer_3_out4, demultiplexer_3_out5, demultiplexer_3_out6, demultiplexer_3_out7,
       demultiplexer_3_out8, demultiplexer_3_out9, demultiplexer_3_out10, demultiplexer_3_out11,
       demultiplexer_3_out12, demultiplexer_3_out13, demultiplexer_3_out14, demultiplexer_3_out15;
  wire [7:0] SP_q;
  wire [15:0] multiplexer_1_out, R0_q, R1_q, R2_q, R3_q, R4_q, R5_q, R6_q, R7_q, R8_q, R9_q, R10_q, R11_q,
       R12_q;
  wire [15:8] pull_resistor_1_node;

  Demultiplexer #(.select(4)) demultiplexer_1 (
    .out0(demultiplexer_1_out0), .out1(demultiplexer_1_out1), .out2(demultiplexer_1_out2),
    .out3(demultiplexer_1_out3), .out4(demultiplexer_1_out4), .out5(demultiplexer_1_out5),
    .out6(demultiplexer_1_out6), .out7(demultiplexer_1_out7), .out8(demultiplexer_1_out8),
    .out9(demultiplexer_1_out9), .out10(demultiplexer_1_out10), .out11(demultiplexer_1_out11),
    .out12(demultiplexer_1_out12), .out13(demultiplexer_1_out13), .out14(demultiplexer_1_out14),
    .out15(demultiplexer_1_out15), .in(WE), .sel(WA));
  or or_1 (JMP, RES, IRQ, demultiplexer_1_out15);
  Register #(.width(16)) R0 (.D(DATA), .en(demultiplexer_1_out0), .clk(CLK), .Q(R0_q), .clr(RES));
  Register #(.width(16)) R1 (.D(DATA), .en(demultiplexer_1_out1), .clk(CLK), .Q(R1_q), .clr(RES));
  Register #(.width(16)) R2 (.D(DATA), .en(demultiplexer_1_out2), .clk(CLK), .Q(R2_q), .clr(RES));
  Register #(.width(16)) R3 (.D(DATA), .en(demultiplexer_1_out3), .clk(CLK), .Q(R3_q), .clr(RES));
  Register #(.width(16)) R4 (.D(DATA), .en(demultiplexer_1_out4), .clk(CLK), .Q(R4_q), .clr(RES));
  Register #(.width(16)) R5 (.D(DATA), .en(demultiplexer_1_out5), .clk(CLK), .Q(R5_q), .clr(RES));
  Register #(.width(16)) R6 (.D(DATA), .en(demultiplexer_1_out6), .clk(CLK), .Q(R6_q), .clr(RES));
  Register #(.width(16)) R7 (.D(DATA), .en(demultiplexer_1_out7), .clk(CLK), .Q(R7_q), .clr(RES));
  Register #(.width(16)) R8 (.D(DATA), .en(demultiplexer_1_out8), .clk(CLK), .Q(R8_q), .clr(RES));
  Register #(.width(16)) R9 (.D(DATA), .en(demultiplexer_1_out9), .clk(CLK), .Q(R9_q), .clr(RES));
  Register #(.width(16)) R10 (.D(DATA), .en(demultiplexer_1_out10), .clk(CLK), .Q(R10_q), .clr(RES));
  Register #(.width(16)) R11 (.D(DATA), .en(demultiplexer_1_out11), .clk(CLK), .Q(R11_q), .clr(RES));
  Register #(.width(16)) R12 (.D(DATA), .en(demultiplexer_1_out12), .clk(CLK), .Q(R12_q), .clr(RES));
  Register SP (.D(DATA[7:0]), .en(demultiplexer_1_out13), .clk(CLK), .Q(SP_q), .clr(RES));
  Multiplexer #(.select(2), .width(16)) multiplexer_1 (
    .in0(DATA), .in1(16'hf700), .in2(16'h8000), .in3(16'hf700), .out(multiplexer_1_out), .sel({IRQ, RES}));
  assign B_Q = demultiplexer_2_out0 ? R0_q : 16'bz;  // Controlled_Buffer controlled_buffer_1
  assign A_Q = demultiplexer_3_out0 ? R0_q : 16'bz;  // Controlled_Buffer controlled_buffer_2
  assign B_Q = demultiplexer_2_out1 ? R1_q : 16'bz;  // Controlled_Buffer controlled_buffer_3
  assign A_Q = demultiplexer_3_out1 ? R1_q : 16'bz;  // Controlled_Buffer controlled_buffer_4
  assign B_Q = demultiplexer_2_out2 ? R2_q : 16'bz;  // Controlled_Buffer controlled_buffer_5
  assign A_Q = demultiplexer_3_out2 ? R2_q : 16'bz;  // Controlled_Buffer controlled_buffer_6
  assign B_Q = demultiplexer_2_out3 ? R3_q : 16'bz;  // Controlled_Buffer controlled_buffer_7
  assign A_Q = demultiplexer_3_out3 ? R3_q : 16'bz;  // Controlled_Buffer controlled_buffer_8
  assign B_Q = demultiplexer_2_out4 ? R4_q : 16'bz;  // Controlled_Buffer controlled_buffer_9
  assign A_Q = demultiplexer_3_out4 ? R4_q : 16'bz;  // Controlled_Buffer controlled_buffer_10
  assign B_Q = demultiplexer_2_out5 ? R5_q : 16'bz;  // Controlled_Buffer controlled_buffer_11
  assign A_Q = demultiplexer_3_out5 ? R5_q : 16'bz;  // Controlled_Buffer controlled_buffer_12
  assign B_Q = demultiplexer_2_out6 ? R6_q : 16'bz;  // Controlled_Buffer controlled_buffer_13
  assign A_Q = demultiplexer_3_out6 ? R6_q : 16'bz;  // Controlled_Buffer controlled_buffer_14
  assign B_Q = demultiplexer_2_out7 ? R7_q : 16'bz;  // Controlled_Buffer controlled_buffer_15
  assign A_Q = demultiplexer_3_out7 ? R7_q : 16'bz;  // Controlled_Buffer controlled_buffer_16
  assign B_Q = demultiplexer_2_out8 ? R8_q : 16'bz;  // Controlled_Buffer controlled_buffer_17
  assign A_Q = demultiplexer_3_out8 ? R8_q : 16'bz;  // Controlled_Buffer controlled_buffer_18
  assign B_Q = demultiplexer_2_out9 ? R9_q : 16'bz;  // Controlled_Buffer controlled_buffer_19
  assign A_Q = demultiplexer_3_out9 ? R9_q : 16'bz;  // Controlled_Buffer controlled_buffer_20
  assign B_Q = demultiplexer_2_out10 ? R10_q : 16'bz;  // Controlled_Buffer controlled_buffer_21
  assign A_Q = demultiplexer_3_out10 ? R10_q : 16'bz;  // Controlled_Buffer controlled_buffer_22
  assign B_Q = demultiplexer_2_out11 ? R11_q : 16'bz;  // Controlled_Buffer controlled_buffer_23
  assign A_Q = demultiplexer_3_out11 ? R11_q : 16'bz;  // Controlled_Buffer controlled_buffer_24
  assign B_Q = demultiplexer_2_out12 ? R12_q : 16'bz;  // Controlled_Buffer controlled_buffer_25
  assign A_Q = demultiplexer_3_out12 ? R12_q : 16'bz;  // Controlled_Buffer controlled_buffer_26
  Pull_Resistor pull_resistor_1 (.node({pull_resistor_1_node, SP_q}));
  assign B_Q = demultiplexer_2_out13 ? {pull_resistor_1_node, SP_q} : 16'bz;  // Controlled_Buffer controlled_buffer_27
  assign A_Q = demultiplexer_3_out13 ? {pull_resistor_1_node, SP_q} : 16'bz;  // Controlled_Buffer controlled_buffer_28
  assign B_Q = demultiplexer_2_out14 ? f_q : 16'bz;  // Controlled_Buffer controlled_buffer_29
  // stat_reg SR: pin names not known; wires that end beside it: demultiplexer_1_out14, f_in, DATA, F_W, CLK, IRQ, f_q
  assign A_Q = demultiplexer_3_out14 ? f_q : 16'bz;  // Controlled_Buffer controlled_buffer_30
  assign B_Q = demultiplexer_2_out15 ? PC_D : 16'bz;  // Controlled_Buffer controlled_buffer_31
  PC pc_1 (.W(JMP), .data(multiplexer_1_out), .clk(CLK), .Q(PC_D));  // open: INC
  assign A_Q = demultiplexer_3_out15 ? PC_D : 16'bz;  // Controlled_Buffer controlled_buffer_32
  Demultiplexer #(.select(4)) demultiplexer_2 (
    .out0(demultiplexer_2_out0), .out1(demultiplexer_2_out1), .out2(demultiplexer_2_out2),
    .out3(demultiplexer_2_out3), .out4(demultiplexer_2_out4), .out5(demultiplexer_2_out5),
    .out6(demultiplexer_2_out6), .out7(demultiplexer_2_out7), .out8(demultiplexer_2_out8),
    .out9(demultiplexer_2_out9), .out10(demultiplexer_2_out10), .out11(demultiplexer_2_out11),
    .out12(demultiplexer_2_out12), .out13(demultiplexer_2_out13), .out14(demultiplexer_2_out14),
    .out15(demultiplexer_2_out15), .in(BE), .sel(BA));
  Demultiplexer #(.select(4)) demultiplexer_3 (
    .out0(demultiplexer_3_out0), .out1(demultiplexer_3_out1), .out2(demultiplexer_3_out2),
    .out3(demultiplexer_3_out3), .out4(demultiplexer_3_out4), .out5(demultiplexer_3_out5),
    .out6(demultiplexer_3_out6), .out7(demultiplexer_3_out7), .out8(demultiplexer_3_out8),
    .out9(demultiplexer_3_out9), .out10(demultiplexer_3_out10), .out11(demultiplexer_3_out11),
    .out12(demultiplexer_3_out12), .out13(demultiplexer_3_out13), .out14(demultiplexer_3_out14),
    .out15(demultiplexer_3_out15), .in(AE), .sel(AA));
  // also tied to VCC on the sheet: pull_resistor_1_node[8]
endmodule

module minimal_cpu (
  input  IRQ,
  input  [15:0] D_IN,
  input  DATA_GRANT,
  input  RESET,
  input  CLK,
  input  [15:0] INST,
  input  INST_G,
  input  HALT,
  output INT,
  output [15:0] INST_ADDR,
  output [15:0] STATUS,
  output [15:0] ADDR,
  output [15:0] D_Q,
  output MEM_R,
  output MEM_W,
  output INST_REQ,
  output SOFT_INT
);

  wire A_IMM, AE, and_1_out, and_3_out, and_4_out, and_5_out, and_6_out, and_7_out, and_8_out, B_IMM, BE,
       buffer_1_out, buffer_2_out, buffer_3_out, buffer_4_out, buffer_5_out, buffer_6_out, clk_t, d_ff_1_q,
       d_ff_2_q, d_ff_3_q, DATA_REQ, edge_detector2_1_q, F_W, HALT_t, IRQ_t, IS_COND, JMP, nand_1_out,
       nand_2_out, nand_3_out, nand_4_out, nand_5_out, nand_6_out, nor_2_out, not_1_out, or_1_out, or_2_out,
       or_3_out, or_4_out, pla_1_out, WE;
  wire [0:0] reg_file2_1_pc_d;
  wire [1:0] controll_unit_data;
  wire [3:0] AA, alu_1_flags, BA, M_OP, WA;
  wire [15:0] alu_1_q, reg_file2_1_a_q;
  wire [31:0] inst_l_q, INST_t;

  nand nand_1 (nand_1_out, ~DATA_GRANT, DATA_REQ);  // NAND_Gate
  nor nor_1 (INST_REQ, nand_5_out, JMP, HALT_t);
  nand nand_2 (nand_2_out, CLK, INST_G);
  PLA #(.in_width(8), .out_width(1), .\table ("0000xxxx 1 # JMP\n0001xxx1 1 # Z = 1\n0010xx1x 1 # N = 1\n0011xx0x 1 # N = 0\n0100x1xx 1 # C = 1\n0101x0xx 1 # C = 0\n0110xxx0 1 # Z = 0\n01111x1x 1 # S >\n01110x0x 1 # S >\n10000x1x 1 # S ≤\n10001x0x 1 # S ≤\n1000xxx1 1 # S ≤\n1001x0xx 1 # !(C & Z)\n1001xxx0 1 # !(C & Z)\n1010x1xx 1 # C | Z = 1\n1010xxx1 1 # C | Z = 1\n1011xx0x 1 # !(N & Z)\n1011xxx0 1 # !(N & Z)\n11001xxx 1 # OV = 1\n11010xxx 1 # OV = 0\nxxxxxxxx 0 # else")) pla_1 (
    .in({INST_t[11:8], STATUS[3:0]}), .out(pla_1_out));
  and and_1 (and_1_out, pla_1_out, WE);
  D_Flip_Flop #(.trigger("falling")) d_ff_1 (.D(nand_1_out), .clk(CLK), .Q(d_ff_1_q));  // open: Qn, preset, reset
  or or_1 (or_1_out, JMP, nand_5_out);
  Pull_Resistor pull_resistor_1 (.node(INST));
  nand nand_3 (nand_3_out, CLK, nand_4_out);
  nand nand_4 (nand_4_out, nand_3_out, nand_2_out);
  S_R_Flip_Flop s_r_ff_1 (.S(IRQ_t), .R(INT), .clk(clk_t), .Q(INT), .reset(RESET));  // open: Qn, preset
  and and_2 (IRQ_t, ~INT, IRQ, STATUS[4]);  // AND_Gate
  and and_3 (and_3_out, WE, ~IS_COND);  // AND_Gate
  and and_4 (and_4_out, and_1_out, IS_COND);
  and and_5 (and_5_out, d_ff_1_q, ~HALT_t, or_1_out, CLK);  // AND_Gate
  not not_1 (not_1_out, CLK);
  Register #(.width(16)) inst_h (.D(INST), .en(1'b1), .clk(nand_4_out), .Q(inst_l_q[31:16]), .clr(JMP));
  Register #(.width(16)) inst_l (.D(INST), .en(1'b1), .clk(nand_3_out), .Q(inst_l_q[15:0]), .clr(JMP));
  and and_6 (and_6_out, nand_5_out, clk_t);
  D_Flip_Flop d_ff_2 (.D(or_2_out), .clk(CLK), .Q(d_ff_2_q), .reset(and_6_out));  // open: Qn, preset
  or or_2 (or_2_out, d_ff_2_q, INST_G);
  D_Flip_Flop #(.trigger("falling")) d_ff_3 (
    .D(or_3_out), .clk(CLK), .Q(d_ff_3_q), .reset(and_6_out));  // open: Qn, preset
  or or_3 (or_3_out, d_ff_3_q, INST_G);
  or or_4 (or_4_out, and_3_out, and_4_out);
  buf buffer_1 (buffer_1_out, buffer_4_out);
  buf buffer_2 (buffer_2_out, buffer_1_out);
  nor nor_2 (nor_2_out, and_5_out, clk_t);
  buf buffer_3 (buffer_3_out, clk_t);
  buf buffer_4 (buffer_4_out, buffer_3_out);
  nor nor_3 (clk_t, nor_2_out, not_1_out);
  and and_7 (and_7_out, INT, ~edge_detector2_1_q);  // AND_Gate
  edge_detector2 edge_detector2_1 (.HIGH(1'b1), .LOW(1'b0), .CLK(clk_t), .Q(edge_detector2_1_q));
  Register #(.width(32)) IR (.D(inst_l_q), .en(1'b1), .clk(buffer_6_out), .Q(INST_t), .clr(RESET));
  buf buffer_5 (buffer_5_out, buffer_2_out);
  buf buffer_6 (buffer_6_out, buffer_5_out);
  nand nand_5 (nand_5_out, nand_6_out, nand_6_out);
  nand nand_6 (nand_6_out, d_ff_2_q, d_ff_3_q);
  reg_file2 reg_file2_1 (
    .RES(RESET), .IRQ(and_7_out), .CLK(buffer_6_out), .f_in(alu_1_flags), .F_W(F_W), .DATA(alu_1_q), .AE(AE),
    .BE(BE), .BA(BA), .AA(AA), .WA(WA), .WE(or_4_out), .JMP(JMP), .B_Q(D_IN), .A_Q(reg_file2_1_a_q),
    .f_q(STATUS), .PC_D({INST_ADDR[15:1], reg_file2_1_pc_d[0]}));
  assign D_IN = B_IMM ? INST_t[31:16] : 16'bz;  // Controlled_Buffer controlled_buffer_1
  assign reg_file2_1_a_q = A_IMM ? INST_t[31:16] : 16'bz;  // Controlled_Buffer controlled_buffer_2
  Pull_Resistor pull_resistor_2 (.node(reg_file2_1_a_q));
  ROM #(.dataWidth(16)) controll_unit (
    .addr(INST_t[7:0]),
    .data({F_W, BE, AE, WE, B_IMM, MEM_R, MEM_W, M_OP, A_IMM, IS_COND, SOFT_INT, controll_unit_data}));
  // Multiplexer #(.select(2), .width(4)) multiplexer_1: pin names not known; wires that end beside it: INST_t[23:20], INST_t[11:8], 4'b0000, INST_t[15:12], WA
  // Multiplexer #(.select(2), .width(4)) multiplexer_2: pin names not known; wires that end beside it: INST_t[15:12], INST_t[15:12], INST_t[15:12], 4'b0000, AA
  Multiplexer #(.select(2), .width(4)) multiplexer_3 (
    .in0(INST_t[19:16]), .in1(4'b0000), .in2(4'b0000), .in3(INST_t[15:12]), .out(BA));  // open: sel
  assign ADDR = INST_G ? {INST_ADDR[15:1], CLK} : 16'bz;  // Controlled_Buffer controlled_buffer_3
  assign ADDR = DATA_GRANT ? reg_file2_1_a_q : 16'bz;  // Controlled_Buffer controlled_buffer_4
  ALU alu_1 (.c_in(STATUS[2]), .b(D_IN), .a(reg_file2_1_a_q), .M_OP(M_OP), .Q(alu_1_q), .FLAGS(alu_1_flags));
  or or_5 (DATA_REQ, MEM_R, MEM_W);
  and and_8 (and_8_out, controll_unit_data[1], ~INT);  // AND_Gate
  or or_6 (HALT_t, and_8_out, HALT);

  assign D_Q = D_IN;
  assign INST_ADDR[0] = CLK;

  // Other names for the same wires on the sheet: PC_ADDR[15:0] = {INST_ADDR[15:1], CLK}; D_G = DATA_GRANT;
  //   res = RESET

  // Notes on the sheet:
  //   contents of controll_unit (hex, n*v repeats v):
  //   0 b800 a848 19c8 f008 b820 a8e8 15d8 f028 b840 b808 43d8 f048 b860 b808 4 0 b8c0 0 2 0 b8e0 0 0 f068
  //   b900 0 0 f0c8 0 0 0 f0e8 0 0 0 f108 0 0 0 e040 0 0 0 e0e0 0 0 0 51c8 0 0 0 d088 0 0 0 d0a8 0 0 0
  //   b128 0 0 0 b148 0 0 0 b168 0 0 0 b188 0 0 0 b1a8 0 0 0 35c8 0 0 0 63c8
endmodule

module stat_reg (
  input  INT,
  input  f_w,
  input  [3:0] ALU_F,
  input  [15:0] BUS_DATA,
  input  alu_e,
  input  CLK,
  input  RES,
  output [15:0] BUS_Q
);

  wire or_1_out;
  wire [15:0] and_1_out, bit_extender_1_out, multiplexer_1_out;

  assign bit_extender_1_out = {{12{1'b0}}, ALU_F};  // Bit_Extender bit_extender_1
  Multiplexer #(.select(2), .width(16)) multiplexer_1 (
    .in0(bit_extender_1_out), .in1(BUS_DATA), .in2(and_1_out), .out(multiplexer_1_out));  // open: in3, sel
  assign and_1_out = 16'hffef & BUS_Q;  // AND_Gate and_1, 16 bits wide
  Register #(.width(16)) SR (.D(multiplexer_1_out), .en(or_1_out), .clk(CLK), .Q(BUS_Q), .clr(RES));
  or or_1 (or_1_out, INT, f_w, alu_e);
endmodule

module MMU (
  input  CPU_CLK,
  input  ROM_CLK,
  input  INST_CLK,
  input  D_REQ,
  input  ROM_REQ,
  input  INST_REQ,
  input  res,
  output CLK_OUT,
  output D_GRANT,
  output ROM_GRANT,
  output INST_GRANT
);

  wire and_2_out, and_3_out, buffer_1_out, buffer_2_out, buffer_3_out, buffer_4_out, buffer_5_out,
       buffer_6_out, buffer_7_out, buffer_8_out, buffer_9_out, buffer_10_out, buffer_11_out, buffer_12_out,
       buffer_13_out, buffer_14_out, counter_1_carry, decoder_1_out0, decoder_1_out1, decoder_1_out2,
       egde_detector_1_q, multiplexer_1_out, or_1_out, or_2_out, por_1_out, req_check_1_inc, req_check_1_req,
       xnor_1_out;
  wire [1:0] counter_2_q;

  and and_1 (CLK_OUT, multiplexer_1_out, req_check_1_req);
  Multiplexer #(.select(2)) multiplexer_1 (
    .in0(CPU_CLK), .in1(ROM_CLK), .in2(INST_CLK), .out(multiplexer_1_out));  // open: in3, sel
  Counter #(.max('hf), .width(4)) counter_1 (
    .load(1'b0), .count(and_2_out), .carry(counter_1_carry), .up(1'b1), .clk(multiplexer_1_out),
    .clr(or_1_out));  // open: D, Q
  or or_1 (or_1_out, res, or_2_out);
  and and_2 (and_2_out, req_check_1_req, xnor_1_out);
  Counter #(.max('h2), .width(2)) counter_2 (
    .load(1'b0), .count(1'b1), .Q(counter_2_q), .up(1'b1), .clk(or_2_out), .clr(1'b0));  // open: D, carry
  or or_2 (or_2_out, counter_1_carry, and_3_out);
  EGDE_DETECTOR egde_detector_1 (.HIGH(1'b1), .LOW(1'b1), .CLK(counter_2_q[0]), .Q(egde_detector_1_q));
  buf buffer_1 (buffer_1_out, egde_detector_1_q);
  buf buffer_2 (buffer_2_out, buffer_1_out);
  POR #(.PorHighDuration(1), .porsize(2)) por_1 (.out(por_1_out));
  and and_3 (and_3_out, ~buffer_2_out, ~por_1_out, req_check_1_inc);  // AND_Gate
  Decoder #(.select(2)) decoder_1 (
    .out0(decoder_1_out0), .out1(decoder_1_out1), .out2(decoder_1_out2), .sel(counter_2_q), .en(1'b1));  // open: out3
  NotExactlyOne xnor_1 (.out(xnor_1_out), .in0(INST_REQ), .in1(ROM_REQ), .in2(D_REQ));
  buf buffer_3 (buffer_3_out, buffer_6_out);
  buf buffer_4 (buffer_4_out, buffer_3_out);
  buf buffer_5 (buffer_5_out, decoder_1_out0);
  buf buffer_6 (buffer_6_out, buffer_5_out);
  buf buffer_7 (buffer_7_out, buffer_10_out);
  buf buffer_8 (buffer_8_out, buffer_7_out);
  buf buffer_9 (buffer_9_out, decoder_1_out1);
  buf buffer_10 (buffer_10_out, buffer_9_out);
  buf buffer_11 (buffer_11_out, buffer_14_out);
  buf buffer_12 (buffer_12_out, buffer_11_out);
  buf buffer_13 (buffer_13_out, decoder_1_out2);
  buf buffer_14 (buffer_14_out, buffer_13_out);
  and and_4 (D_GRANT, buffer_4_out, ~req_check_1_inc);  // AND_Gate
  and and_5 (ROM_GRANT, buffer_8_out, ~req_check_1_inc);  // AND_Gate
  and and_6 (INST_GRANT, buffer_12_out, ~req_check_1_inc);  // AND_Gate
  REQ_CHECK req_check_1 (
    .D_REQ(D_REQ), .ROM_REQ(ROM_REQ), .INST_REQ(INST_REQ), .D_GRANT(decoder_1_out0),
    .ROM_GRANT(decoder_1_out1), .INST_GRANT(decoder_1_out2), .INC(req_check_1_inc), .req(req_check_1_req));
endmodule

module REQ_CHECK (
  input  D_REQ,
  input  ROM_REQ,
  input  INST_REQ,
  input  D_GRANT,
  input  ROM_GRANT,
  input  INST_GRANT,
  output INC,
  output req
);

  wire and_1_out, and_2_out, and_3_out, and_4_out, buffer_1_out, not_1_out, not_2_out, not_3_out, or_1_out,
       or_2_out;

  or or_1 (or_1_out, D_REQ, ROM_REQ, INST_REQ);
  buf buffer_1 (buffer_1_out, or_1_out);
  buf buffer_2 (req, buffer_1_out);
  not not_1 (not_1_out, D_REQ);
  not not_2 (not_2_out, ROM_REQ);
  not not_3 (not_3_out, INST_REQ);
  and and_1 (and_1_out, D_REQ, ~D_GRANT, INST_GRANT);  // AND_Gate
  and and_2 (and_2_out, not_1_out, D_GRANT);
  and and_3 (and_3_out, not_2_out, ROM_GRANT);
  and and_4 (and_4_out, not_3_out, INST_GRANT);
  or or_2 (or_2_out, and_1_out, and_2_out, and_3_out, and_4_out);
  and and_5 (INC, req, or_2_out);
endmodule

module EGDE_DETECTOR (
  input  HIGH,
  input  LOW,
  input  CLK,
  output Q
);

  wire and_1_out, and_2_out, and_3_out, nor_1_out, not_1_out, not_2_out;

  not not_1 (not_1_out, CLK);
  not not_2 (not_2_out, CLK);
  and and_1 (and_1_out, CLK, not_1_out);
  and and_2 (and_2_out, and_1_out, HIGH);
  nor nor_1 (nor_1_out, CLK, not_2_out);
  and and_3 (and_3_out, nor_1_out, LOW);
  or or_1 (Q, and_2_out, and_3_out);
endmodule

module ROM_CPU (
  input  START_WE,
  input  TRANSFER_GRANT,
  input  [15:0] ADDR,
  input  FINISH_WE,
  input  CLK,
  input  WE_CLK,
  input  DONE_ACCEPTED,
  output [15:0] ADDRESS,
  output DONE,
  output ROM_REQ,
  output active
);

  wire and_1_out, and_2_out, and_3_out, and_4_out, and_5_out, comparator_1_eq, d_ff_1_q, d_ff_2_q,
       multiplexer_1_out;
  wire [15:0] adder_1_out, register_1_q;

  and and_1 (and_1_out, ~active, START_WE);  // AND_Gate
  Counter #(.max('hffff), .width(16)) counter_1 (
    .load(and_1_out), .D(ADDR), .count(and_5_out), .Q(ADDRESS), .up(1'b1), .clk(multiplexer_1_out), .clr(1'b0));  // open: carry
  Multiplexer multiplexer_1 (.in0(CLK), .in1(WE_CLK), .out(multiplexer_1_out), .sel(and_1_out));
  D_Flip_Flop d_ff_1 (.D(and_1_out), .clk(and_2_out), .Q(d_ff_1_q), .reset(DONE_ACCEPTED));  // open: Qn, preset
  and and_2 (and_2_out, and_1_out, WE_CLK);
  Register #(.trigger("falling"), .width(16)) register_1 (
    .D(adder_1_out), .en(and_3_out), .clk(WE_CLK), .Q(register_1_q), .clr(1'b0));
  Adder #(.width(16)) adder_1 (.a(ADDRESS), .b(ADDR), .out(adder_1_out), .cin(1'b0));  // open: cout
  and and_3 (and_3_out, ~active, FINISH_WE);  // AND_Gate
  and and_4 (and_4_out, and_3_out, WE_CLK);
  and and_5 (and_5_out, active, TRANSFER_GRANT);
  D_Flip_Flop d_ff_2 (.D(and_3_out), .clk(and_4_out), .Q(d_ff_2_q), .reset(DONE_ACCEPTED));  // open: Qn, preset
  and and_6 (active, d_ff_1_q, d_ff_2_q);
  Comparator #(.mode("unsigned"), .width(16)) comparator_1 (
    .a(ADDRESS), .b(register_1_q), .eq(comparator_1_eq));  // open: gt, lt
  and and_7 (DONE, comparator_1_eq, active);
  and and_8 (ROM_REQ, active, ~comparator_1_eq);  // AND_Gate
endmodule

module edge_detector2 (
  input  HIGH,
  input  LOW,
  input  CLK,
  output Q
);

  wire and_1_out, and_2_out, and_3_out, nor_1_out, not_1_out, not_2_out, not_3_out, not_4_out, not_5_out,
       not_6_out;

  not not_1 (not_1_out, CLK);
  not not_2 (not_2_out, not_1_out);
  not not_3 (not_3_out, not_2_out);
  not not_4 (not_4_out, CLK);
  not not_5 (not_5_out, not_4_out);
  not not_6 (not_6_out, not_5_out);
  and and_1 (and_1_out, CLK, not_3_out);
  and and_2 (and_2_out, and_1_out, HIGH);
  nor nor_1 (nor_1_out, CLK, not_6_out);
  and and_3 (and_3_out, nor_1_out, LOW);
  or or_1 (Q, and_2_out, and_3_out);
endmodule

module MEM_ARBITER (
  input  INST_GRANT,
  input  D_GRANT,
  input  ROM_GRANT,
  input  CPU_R,
  input  CPU_W,
  output MEM_R,
  output MEM_W
);

  wire and_1_out, and_2_out;

  and and_1 (and_1_out, CPU_R, D_GRANT);
  and and_2 (and_2_out, CPU_W, D_GRANT);
  or or_1 (MEM_R, and_1_out, INST_GRANT);
  or or_2 (MEM_W, ROM_GRANT, and_2_out);
endmodule

module S_R_L (
  input  POR_RES,
  input  SET,
  input  RESET,
  output Q
);

  wire and_1_out, and_2_out, nor_1_out, or_1_out, or_2_out, por_1_out;

  POR #(.PorHighDuration(1), .porsize(2)) por_1 (.out(por_1_out));
  and and_1 (and_1_out, ~POR_RES, por_1_out);  // AND_Gate
  and and_2 (and_2_out, POR_RES, por_1_out);
  or or_1 (or_1_out, SET, and_1_out);
  nor nor_1 (nor_1_out, or_1_out, Q);
  nor nor_2 (Q, nor_1_out, or_2_out);
  or or_2 (or_2_out, and_2_out, RESET);
endmodule

module INST_BUFFER (
  input  [15:0] D,
  input  INST_H_W,
  input  CLK,
  input  JMP,
  input  RES,
  input  INST_L_W,
  output INST_L_REQ,
  output [31:0] Q,
  output HAS_INST
);

  wire edge_detector2_1_q, or_1_out;
  wire [15:0] INST_H_q;
  wire [31:0] multiplexer_1_out;

  D_Flip_Flop #(.trigger("high")) d_ff_1 (.D(INST_H_W), .clk(CLK), .Q(INST_L_REQ), .reset(JMP));  // open: Qn, preset
  Register #(.trigger("high"), .width(16)) INST_H (.D(D), .en(INST_H_W), .clk(CLK), .Q(INST_H_q), .clr(JMP));
  or or_1 (or_1_out, RES, INST_L_W);
  Register #(.trigger("falling"), .width(32)) register_1 (
    .D(multiplexer_1_out), .en(or_1_out), .clk(CLK), .Q(Q), .clr(JMP));
  Multiplexer #(.width(32)) multiplexer_1 (.in0({INST_H_q, D}), .in1(32'hf700f003), .out(multiplexer_1_out), .sel(RES));
  S_R_Flip_Flop #(.trigger("falling")) s_r_ff_1 (
    .S(or_1_out), .R(1'b0), .clk(CLK), .Q(HAS_INST), .reset(edge_detector2_1_q), .preset(1'b0));  // open: Qn
  edge_detector2 edge_detector2_1 (.HIGH(1'b1), .LOW(1'b0), .CLK(CLK), .Q(edge_detector2_1_q));

  // Notes on the sheet:
  //   jmp reset vector
endmodule

module SMAL_AND (
  input  A,
  input  B,
  output Q
);

  and and_1 (Q, A, B);
endmodule

module req_manage (
  input  d_g,
  input  d_req,
  input  clk,
  output Q
);

  wire and_1_out, not_1_out, not_2_out;

  not not_1 (not_1_out, clk);
  not not_2 (not_2_out, d_req);
  and and_1 (and_1_out, d_req, d_g, not_1_out);
  or or_1 (Q, not_2_out, and_1_out);
endmodule

module IS_EQ (
  input  [15:0] A,
  input  [15:0] B,
  output EQ
);

  wire [15:0] xor_1_out;

  assign xor_1_out = A ^ B;  // XOR_Gate xor_1, 16 bits wide
  nor nor_1 (EQ, 1'b0, xor_1_out[0], xor_1_out[1], xor_1_out[2], xor_1_out[3], xor_1_out[4], xor_1_out[5], xor_1_out[6], xor_1_out[7], xor_1_out[8], xor_1_out[9], xor_1_out[10], xor_1_out[11], xor_1_out[12], xor_1_out[13], xor_1_out[14], xor_1_out[15]);
endmodule

module brb_cpu (
  input  [15:0] D_IN,
  input  DATA_GRANT,
  input  clk,
  input  res,
  input  INST_G,
  input  HALT,
  input  IRQ,
  output [15:0] D_Q,
  output [15:0] ADDR,
  output INST_REQ,
  output MEM_R,
  output MEM_W,
  output SOFT_INT,
  output [15:0] STATUS,
  output [15:0] INST_ADDR,
  output INT
);

  wire A_IMM, adder_1_cout, AE, and_1_out, and_2_out, and_3_out, and_5_out, and_6_out, and_7_out, and_8_out,
       and_9_out, and_10_out, and_11_out, and_12_out, B_IMM, BE, buffer_1_out, buffer_2_out, buffer_3_out,
       cpu_clk, d_ff_1_q, DATA_REQ, demultiplexer_1_out0, demultiplexer_1_out1, demultiplexer_1_out2,
       demultiplexer_1_out3, demultiplexer_1_out4, demultiplexer_1_out5, demultiplexer_1_out6,
       demultiplexer_1_out7, demultiplexer_1_out8, demultiplexer_1_out9, demultiplexer_1_out10,
       demultiplexer_1_out11, demultiplexer_1_out12, demultiplexer_1_out13, demultiplexer_1_out14,
       demultiplexer_1_out15, demultiplexer_2_out0, demultiplexer_2_out1, demultiplexer_2_out2,
       demultiplexer_2_out3, demultiplexer_2_out4, demultiplexer_2_out5, demultiplexer_2_out6,
       demultiplexer_2_out7, demultiplexer_2_out8, demultiplexer_2_out9, demultiplexer_2_out10,
       demultiplexer_2_out11, demultiplexer_2_out12, demultiplexer_2_out13, demultiplexer_2_out14,
       demultiplexer_2_out15, demultiplexer_3_out0, demultiplexer_3_out1, demultiplexer_3_out2,
       demultiplexer_3_out3, demultiplexer_3_out4, demultiplexer_3_out5, demultiplexer_3_out6,
       demultiplexer_3_out7, demultiplexer_3_out8, demultiplexer_3_out9, demultiplexer_3_out10,
       demultiplexer_3_out11, demultiplexer_3_out12, demultiplexer_3_out13, demultiplexer_3_out14,
       demultiplexer_3_out15, F_W, H_out, HALT_t, INT_RET_REG_BE, IRQ_t, IS_COND, JMP, L_out,
       multiplexer_7_out, nand_1_out, nand_2_out, nand_3_out, nand_4_out, nand_5_out, nand_6_out, nand_7_out,
       nand_8_out, nor_2_out, not_1_out, not_2_out, not_3_out, not_4_out, not_cpu_clk, or_1_out, or_3_out,
       or_4_out, or_5_out, pla_1_out, WE, xor_1_out, xor_2_out;
  wire [0:0] PC_ADDR;
  wire [1:0] c_op, sh_op;
  wire [1:1] controll_unit_data;
  wire [2:0] rom_1_data;
  wire [3:0] AA, alu_f, BA, M_OP, WA;
  wire [7:0] SP_q;
  wire [14:0] adder_1_out;
  wire [15:0] a, b, controlled_buffer_1_out, multiplexer_1_out, multiplexer_5_out, R0_q, R1_q, R2_q, R3_q,
       R4_q, R5_q, R6_q, R7_q, R8_q, R9_q, R10_q, R11_q, R12_q, register_1_q, register_2_q;
  wire [15:8] pull_resistor_1_node;
  wire [15:15] multiplexer_6_out;
  wire [31:0] INST, register_3_q;

  PLA #(.in_width(8), .out_width(1), .\table ("0000xxxx 1 # JMP\n0001xxx1 1 # Z = 1\n0010xx1x 1 # N = 1\n0011xx0x 1 # N = 0\n0100x1xx 1 # C = 1\n0101x0xx 1 # C = 0\n0110xxx0 1 # Z = 0\n01111x1x 1 # S >\n01110x0x 1 # S >\n10000x1x 1 # S ≤\n10001x0x 1 # S ≤\n1000xxx1 1 # S ≤\n1001x0xx 1 # !(C & Z)\n1001xxx0 1 # !(C & Z)\n1010x1xx 1 # C | Z = 1\n1010xxx1 1 # C | Z = 1\n1011xx0x 1 # !(N & Z)\n1011xxx0 1 # !(N & Z)\n11001xxx 1 # OV = 1\n11010xxx 1 # OV = 0\nxxxxxxxx 0 # else")) pla_1 (
    .in({INST[11:8], STATUS[3:0]}), .out(pla_1_out));
  and and_1 (and_1_out, WE, ~IS_COND);  // AND_Gate
  and and_2 (and_2_out, pla_1_out, WE);
  and and_3 (and_3_out, and_2_out, IS_COND);
  or or_1 (or_1_out, and_1_out, and_3_out);
  Demultiplexer #(.select(4)) demultiplexer_1 (
    .out0(demultiplexer_1_out0), .out1(demultiplexer_1_out1), .out2(demultiplexer_1_out2),
    .out3(demultiplexer_1_out3), .out4(demultiplexer_1_out4), .out5(demultiplexer_1_out5),
    .out6(demultiplexer_1_out6), .out7(demultiplexer_1_out7), .out8(demultiplexer_1_out8),
    .out9(demultiplexer_1_out9), .out10(demultiplexer_1_out10), .out11(demultiplexer_1_out11),
    .out12(demultiplexer_1_out12), .out13(demultiplexer_1_out13), .out14(demultiplexer_1_out14),
    .out15(demultiplexer_1_out15), .in(or_1_out), .sel(WA));
  and and_4 (IRQ_t, ~INT, IRQ, STATUS[4]);  // AND_Gate
  S_R_Flip_Flop s_r_ff_1 (.S(IRQ_t), .R(INT), .clk(cpu_clk), .Q(INT), .reset(res));  // open: Qn, preset
  or or_2 (JMP, res, INT, demultiplexer_1_out15);
  Register #(.width(16)) register_1 (.D(INST_ADDR), .en(INT), .clk(INT), .Q(register_1_q), .clr(res));
  Register #(.width(16)) R0 (
    .D({alu_f[1], adder_1_out}), .en(demultiplexer_1_out0), .clk(cpu_clk), .Q(R0_q), .clr(res));
  Register #(.width(16)) R1 (
    .D({alu_f[1], adder_1_out}), .en(demultiplexer_1_out1), .clk(cpu_clk), .Q(R1_q), .clr(res));
  Register #(.width(16)) R2 (
    .D({alu_f[1], adder_1_out}), .en(demultiplexer_1_out2), .clk(cpu_clk), .Q(R2_q), .clr(res));
  Register #(.width(16)) R3 (
    .D({alu_f[1], adder_1_out}), .en(demultiplexer_1_out3), .clk(cpu_clk), .Q(R3_q), .clr(res));
  Register #(.width(16)) R4 (
    .D({alu_f[1], adder_1_out}), .en(demultiplexer_1_out4), .clk(cpu_clk), .Q(R4_q), .clr(res));
  Register #(.width(16)) R5 (
    .D({alu_f[1], adder_1_out}), .en(demultiplexer_1_out5), .clk(cpu_clk), .Q(R5_q), .clr(res));
  Register #(.width(16)) R6 (
    .D({alu_f[1], adder_1_out}), .en(demultiplexer_1_out6), .clk(cpu_clk), .Q(R6_q), .clr(res));
  Register #(.width(16)) R7 (
    .D({alu_f[1], adder_1_out}), .en(demultiplexer_1_out7), .clk(cpu_clk), .Q(R7_q), .clr(res));
  Register #(.width(16)) R8 (
    .D({alu_f[1], adder_1_out}), .en(demultiplexer_1_out8), .clk(cpu_clk), .Q(R8_q), .clr(res));
  Register #(.width(16)) R9 (
    .D({alu_f[1], adder_1_out}), .en(demultiplexer_1_out9), .clk(cpu_clk), .Q(R9_q), .clr(res));
  Register #(.width(16)) R10 (
    .D({alu_f[1], adder_1_out}), .en(demultiplexer_1_out10), .clk(cpu_clk), .Q(R10_q), .clr(res));
  Register #(.width(16)) R11 (
    .D({alu_f[1], adder_1_out}), .en(demultiplexer_1_out11), .clk(cpu_clk), .Q(R11_q), .clr(res));
  Register #(.width(16)) R12 (
    .D({alu_f[1], adder_1_out}), .en(demultiplexer_1_out12), .clk(cpu_clk), .Q(R12_q), .clr(res));
  Register SP (.D(adder_1_out[7:0]), .en(demultiplexer_1_out13), .clk(cpu_clk), .Q(SP_q), .clr(res));
  Multiplexer #(.select(2), .width(16)) multiplexer_1 (
    .in0({alu_f[1], adder_1_out}), .in1(16'hf700), .in2(16'h8000), .in3(16'hf700), .out(multiplexer_1_out),
    .sel({INT, res}));
  not not_1 (not_1_out, DATA_REQ);
  assign controlled_buffer_1_out = INT_RET_REG_BE ? register_1_q : 16'bz;  // Controlled_Buffer controlled_buffer_1
  assign controlled_buffer_1_out = demultiplexer_2_out0 ? R0_q : 16'bz;  // Controlled_Buffer controlled_buffer_2
  assign a = demultiplexer_3_out0 ? R0_q : 16'bz;  // Controlled_Buffer controlled_buffer_3
  assign controlled_buffer_1_out = demultiplexer_2_out1 ? R1_q : 16'bz;  // Controlled_Buffer controlled_buffer_4
  assign a = demultiplexer_3_out1 ? R1_q : 16'bz;  // Controlled_Buffer controlled_buffer_5
  assign controlled_buffer_1_out = demultiplexer_2_out2 ? R2_q : 16'bz;  // Controlled_Buffer controlled_buffer_6
  assign a = demultiplexer_3_out2 ? R2_q : 16'bz;  // Controlled_Buffer controlled_buffer_7
  assign controlled_buffer_1_out = demultiplexer_2_out3 ? R3_q : 16'bz;  // Controlled_Buffer controlled_buffer_8
  assign a = demultiplexer_3_out3 ? R3_q : 16'bz;  // Controlled_Buffer controlled_buffer_9
  assign controlled_buffer_1_out = demultiplexer_2_out4 ? R4_q : 16'bz;  // Controlled_Buffer controlled_buffer_10
  assign a = demultiplexer_3_out4 ? R4_q : 16'bz;  // Controlled_Buffer controlled_buffer_11
  assign controlled_buffer_1_out = demultiplexer_2_out5 ? R5_q : 16'bz;  // Controlled_Buffer controlled_buffer_12
  assign a = demultiplexer_3_out5 ? R5_q : 16'bz;  // Controlled_Buffer controlled_buffer_13
  assign controlled_buffer_1_out = demultiplexer_2_out6 ? R6_q : 16'bz;  // Controlled_Buffer controlled_buffer_14
  assign a = demultiplexer_3_out6 ? R6_q : 16'bz;  // Controlled_Buffer controlled_buffer_15
  assign controlled_buffer_1_out = demultiplexer_2_out7 ? R7_q : 16'bz;  // Controlled_Buffer controlled_buffer_16
  assign a = demultiplexer_3_out7 ? R7_q : 16'bz;  // Controlled_Buffer controlled_buffer_17
  assign controlled_buffer_1_out = demultiplexer_2_out8 ? R8_q : 16'bz;  // Controlled_Buffer controlled_buffer_18
  assign a = demultiplexer_3_out8 ? R8_q : 16'bz;  // Controlled_Buffer controlled_buffer_19
  assign controlled_buffer_1_out = demultiplexer_2_out9 ? R9_q : 16'bz;  // Controlled_Buffer controlled_buffer_20
  assign a = demultiplexer_3_out9 ? R9_q : 16'bz;  // Controlled_Buffer controlled_buffer_21
  assign controlled_buffer_1_out = demultiplexer_2_out10 ? R10_q : 16'bz;  // Controlled_Buffer controlled_buffer_22
  assign a = demultiplexer_3_out10 ? R10_q : 16'bz;  // Controlled_Buffer controlled_buffer_23
  assign controlled_buffer_1_out = demultiplexer_2_out11 ? R11_q : 16'bz;  // Controlled_Buffer controlled_buffer_24
  assign a = demultiplexer_3_out11 ? R11_q : 16'bz;  // Controlled_Buffer controlled_buffer_25
  assign controlled_buffer_1_out = demultiplexer_2_out12 ? R12_q : 16'bz;  // Controlled_Buffer controlled_buffer_26
  assign a = demultiplexer_3_out12 ? R12_q : 16'bz;  // Controlled_Buffer controlled_buffer_27
  Pull_Resistor pull_resistor_1 (.node({pull_resistor_1_node, SP_q}));
  Pull_Resistor pull_resistor_2 (.node(controlled_buffer_1_out));
  Pull_Resistor pull_resistor_3 (.node(a));
  assign controlled_buffer_1_out = demultiplexer_2_out13 ? {pull_resistor_1_node, SP_q} : 16'bz;  // Controlled_Buffer controlled_buffer_28
  assign a = demultiplexer_3_out13 ? {pull_resistor_1_node, SP_q} : 16'bz;  // Controlled_Buffer controlled_buffer_29
  stat_reg SR (
    .INT(INT), .f_w(demultiplexer_1_out14), .ALU_F(alu_f), .BUS_DATA({alu_f[1], adder_1_out}), .alu_e(F_W),
    .CLK(cpu_clk), .RES(res), .BUS_Q(STATUS));
  assign controlled_buffer_1_out = demultiplexer_2_out14 ? STATUS : 16'bz;  // Controlled_Buffer controlled_buffer_30
  assign a = demultiplexer_3_out14 ? STATUS : 16'bz;  // Controlled_Buffer controlled_buffer_31
  assign controlled_buffer_1_out = demultiplexer_2_out15 ? INST_ADDR : 16'bz;  // Controlled_Buffer controlled_buffer_32
  PC pc_1 (.W(JMP), .data(multiplexer_1_out), .clk(not_cpu_clk), .INC(not_1_out), .Q(INST_ADDR));
  assign a = demultiplexer_3_out15 ? INST_ADDR : 16'bz;  // Controlled_Buffer controlled_buffer_33
  buf buffer_1 (buffer_1_out, clk);
  buf buffer_2 (buffer_2_out, buffer_1_out);
  buf buffer_3 (buffer_3_out, buffer_2_out);
  buf buffer_4 (PC_ADDR[0], buffer_3_out);
  Demultiplexer #(.select(4)) demultiplexer_2 (
    .out0(demultiplexer_2_out0), .out1(demultiplexer_2_out1), .out2(demultiplexer_2_out2),
    .out3(demultiplexer_2_out3), .out4(demultiplexer_2_out4), .out5(demultiplexer_2_out5),
    .out6(demultiplexer_2_out6), .out7(demultiplexer_2_out7), .out8(demultiplexer_2_out8),
    .out9(demultiplexer_2_out9), .out10(demultiplexer_2_out10), .out11(demultiplexer_2_out11),
    .out12(demultiplexer_2_out12), .out13(demultiplexer_2_out13), .out14(demultiplexer_2_out14),
    .out15(demultiplexer_2_out15), .in(BE), .sel(BA));
  Demultiplexer #(.select(4)) demultiplexer_3 (
    .out0(demultiplexer_3_out0), .out1(demultiplexer_3_out1), .out2(demultiplexer_3_out2),
    .out3(demultiplexer_3_out3), .out4(demultiplexer_3_out4), .out5(demultiplexer_3_out5),
    .out6(demultiplexer_3_out6), .out7(demultiplexer_3_out7), .out8(demultiplexer_3_out8),
    .out9(demultiplexer_3_out9), .out10(demultiplexer_3_out10), .out11(demultiplexer_3_out11),
    .out12(demultiplexer_3_out12), .out13(demultiplexer_3_out13), .out14(demultiplexer_3_out14),
    .out15(demultiplexer_3_out15), .in(AE), .sel(AA));
  nor nor_1 (INST_REQ, HALT_t, DATA_REQ, or_3_out);
  assign D_Q = and_5_out ? controlled_buffer_1_out : 16'bz;  // Controlled_Buffer controlled_buffer_34
  and and_5 (and_5_out, MEM_W, DATA_GRANT);
  assign controlled_buffer_1_out = and_6_out ? D_IN : 16'bz;  // Controlled_Buffer controlled_buffer_35
  and and_6 (and_6_out, DATA_GRANT, MEM_R);
  and and_7 (and_7_out, DATA_GRANT, DATA_REQ);
  D_Flip_Flop d_ff_1 (.D(and_7_out), .clk(clk), .Q(d_ff_1_q));  // open: Qn, preset, reset
  or or_3 (or_3_out, DATA_REQ, JMP);
  not not_2 (not_2_out, clk);
  or or_4 (or_4_out, d_ff_1_q, nand_3_out, or_3_out);
  and and_8 (and_8_out, or_4_out, ~HALT_t, clk);  // AND_Gate
  not not_3 (not_3_out, clk);
  Pull_Resistor pull_resistor_4 (.node(D_IN));
  Register #(.width(16)) register_2 (.D(D_IN), .en(1'b1), .clk(not_2_out), .Q(register_2_q), .clr(or_3_out));
  not not_4 (not_4_out, or_3_out);
  nand nand_1 (nand_1_out, clk, INST_G);
  nand nand_2 (nand_2_out, L_out, not_2_out, INST_G);
  ROM #(.addrWidth(4), .dataWidth(7)) rom_1 (.addr(M_OP), .data({c_op, sh_op, rom_1_data}));
  nor nor_2 (nor_2_out, and_8_out, not_cpu_clk);
  nor nor_3 (not_cpu_clk, nor_2_out, not_3_out);
  nand nand_3 (nand_3_out, ~nand_4_out, L_out);  // NAND_Gate
  and and_9 (and_9_out, not_4_out, nand_1_out);
  and and_10 (and_10_out, not_4_out, nand_2_out);
  not not_5 (cpu_clk, not_cpu_clk);
  nand nand_4 (nand_4_out, not_cpu_clk, and_11_out);
  and and_11 (and_11_out, L_out, H_out);
  nand L (L_out, and_9_out, nand_5_out);
  nand nand_5 (nand_5_out, L_out, nand_3_out);
  nand H (H_out, and_10_out, nand_6_out);
  nand nand_6 (nand_6_out, H_out, nand_3_out);
  assign controlled_buffer_1_out = B_IMM ? INST[31:16] : 16'bz;  // Controlled_Buffer controlled_buffer_36
  Register #(.width(32)) register_3 (
    .D({D_IN, register_2_q}), .en(1'b1), .clk(nand_8_out), .Q(register_3_q), .clr(JMP));
  nand nand_7 (nand_7_out, not_cpu_clk, nand_8_out);
  nand nand_8 (nand_8_out, nand_7_out, nand_4_out);
  Register #(.width(32)) register_4 (.D(register_3_q), .en(1'b1), .clk(nand_8_out), .Q(INST), .clr(or_5_out));
  or or_5 (or_5_out, res, INT);
  assign a = A_IMM ? INST[31:16] : 16'bz;  // Controlled_Buffer controlled_buffer_37
  ROM #(.addrWidth(19)) rom_2 (.addr({rom_1_data, controlled_buffer_1_out[15:8], a[15:8]}), .data(b[15:8]));
  ROM #(.addrWidth(19)) rom_3 (.addr({rom_1_data, controlled_buffer_1_out[7:0], a[7:0]}), .data(b[7:0]));
  assign ADDR = INST_G ? {INST_ADDR[15:1], PC_ADDR[0]} : 16'bz;  // Controlled_Buffer controlled_buffer_38
  assign ADDR = DATA_GRANT ? a : 16'bz;  // Controlled_Buffer controlled_buffer_39
  ROM #(.dataWidth(16)) controll_unit (
    .addr(INST[7:0]),
    .data({F_W, BE, AE, WE, B_IMM, MEM_R, MEM_W, M_OP, A_IMM, IS_COND, SOFT_INT, controll_unit_data[1], INT_RET_REG_BE}));
  // Multiplexer #(.select(2), .width(4)) multiplexer_2: pin names not known; wires that end beside it: INST[23:20], INST[11:8], 4'b0000, INST[15:12], WA
  // Multiplexer #(.select(2), .width(4)) multiplexer_3: pin names not known; wires that end beside it: INST[15:12], INST[15:12], INST[15:12], 4'b0000, AA
  Multiplexer #(.select(2), .width(4)) multiplexer_4 (
    .in0(INST[19:16]), .in1(4'b0000), .in2(4'b0000), .in3(INST[15:12]), .out(BA));  // open: sel
  or or_6 (DATA_REQ, MEM_R, MEM_W);
  and and_12 (and_12_out, controll_unit_data[1], ~INT);  // AND_Gate
  or or_7 (HALT_t, and_12_out, HALT);
  Multiplexer #(.select(2), .width(16)) multiplexer_5 (
    .in0({16{1'b0}}), .in1({multiplexer_6_out[15], a[15:1]}), .in2({a[14:0], multiplexer_6_out[15]}),
    .in3(a), .out(multiplexer_5_out), .sel(sh_op));
  Multiplexer #(.select(2)) multiplexer_6 (
    .in0(STATUS[2]), .in1(1'b0), .in2(1'b1), .in3(a[15]), .out(multiplexer_6_out[15]));  // open: sel
  Multiplexer #(.select(2)) multiplexer_7 (
    .in0(multiplexer_6_out[15]), .in1(1'b0), .in2(1'b0), .in3(multiplexer_6_out[15]), .out(multiplexer_7_out));  // open: sel
  Adder #(.width(16)) adder_1 (
    .a(multiplexer_5_out), .b(b), .out({alu_f[1], adder_1_out}), .cin(multiplexer_7_out), .cout(adder_1_cout));
  Multiplexer #(.select(2)) multiplexer_8 (
    .in0(adder_1_cout), .in1(a[0]), .in2(a[15]), .in3(adder_1_cout), .out(alu_f[2]));  // open: sel
  nor nor_4 (alu_f[0], alu_f[1], adder_1_out[14], adder_1_out[13], adder_1_out[12], adder_1_out[11], adder_1_out[10], adder_1_out[9], adder_1_out[8], adder_1_out[7], adder_1_out[6], adder_1_out[5], adder_1_out[4], adder_1_out[3], adder_1_out[2], adder_1_out[1], adder_1_out[0], 1'b0);
  xor xor_1 (xor_1_out, a[15], alu_f[1]);
  xor xor_2 (xor_2_out, alu_f[1], b[15]);
  and and_13 (alu_f[3], xor_1_out, xor_2_out);
  // also tied to VCC on the sheet: pull_resistor_1_node[8]

  // Other names for the same wires on the sheet: W = MEM_W; R = MEM_R; D_G = DATA_GRANT; inst_buffer_clk = clk;
  //   PC_ADDR[15:1] = INST_ADDR[15:1]; RET_ADDR[15:0] = INST_ADDR; flags[3:0] = STATUS[3:0]

  // Notes on the sheet:
  //   contents of rom_1 (hex, n*v repeats v):
  //   38 18 59 19 21 41 22 23 24 28 8 30 10 68 20
  //   contents of rom_2 (hex, n*v repeats v):
  //   256*0 256*1 256*2 256*3 256*4 256*5 256*6 256*7 256*8 256*9 256*a 256*b 256*c 256*d 256*e 256*f
  //   256*10 256*11 256*12 256*13 256*14 256*15 256*16 256*17 256*18 256*19 256*1a 256*1b 256*1c 256*1d
  //   256*1e 256*1f 256*20 256*21 256*22 256*23 256*24 256*25 256*26 256*27 256*28 256*29 256*2a 256*2b
  //   256*2c 256*2d 256*2e 256*2f 256*30 256*31 256*32 256*33 256*34 256*35 256*36 256*37 256*38 256*39
  //   256*3a 256*3b 256*3c 256*3d 256*3e 256*3f 256*40 256*41 256*42 256*43 256*44 256*45 256*46 256*47
  //   256*48 256*49 256*4a 256*4b 256*4c 256*4d 256*4e 256*4f 256*50 256*51 256*52 256*53 256*54 256*55
  //   256*56 256*57 256*58 256*59 256*5a 256*5b 256*5c 256*5d 256*5e 256*5f 256*60 256*61 256*62 256*63
  //   256*64 256*65 256*66 256*67 256*68 256*69 256*6a 256*6b 256*6c 256*6d 256*6e 256*6f 256*70 256*71
  //   256*72 256*73 256*74 256*75 256*76 256*77 256*78 256*79 256*7a 256*7b 256*7c 256*7d 256*7e 256*7f
  //   256*80 256*81 256*82 256*83 256*84 256*85 256*86 256*87 256*88 256*89 256*8a 256*8b 256*8c 256*8d
  //   256*8e 256*8f 256*90 256*91 256*92 256*93 256*94 256*95 256*96 256*97 256*98 256*99 256*9a 256*9b
  //   256*9c 256*9d 256*9e 256*9f 256*a0 256*a1 256*a2 256*a3 256*a4 256*a5 256*a6 256*a7 256*a8 256*a9
  //   256*aa 256*ab 256*ac 256*ad 256*ae 256*af 256*b0 256*b1 256*b2 256*b3 256*b4 256*b5 256*b6 256*b7
  //   256*b8 256*b9 256*ba 256*bb 256*bc 256*bd 256*be 256*bf 256*c0 256*c1 256*c2 256*c3 256*c4 256*c5
  //   256*c6 256*c7 256*c8 256*c9 256*ca 256*cb 256*cc 256*cd 256*ce 256*cf 256*d0 256*d1 256*d2 256*d3
  //   256*d4 256*d5 256*d6 256*d7 256*d8 256*d9 256*da 256*db 256*dc 256*dd 256*de 256*df 256*e0 256*e1
  //   256*e2 256*e3 256*e4 256*e5 256*e6 256*e7 256*e8 256*e9 256*ea 256*eb 256*ec 256*ed 256*ee 256*ef
  //   256*f0 256*f1 256*f2 256*f3 256*f4 256*f5 256*f6 256*f7 256*f8 256*f9 256*fa 256*fb 256*fc 256*fd
  //   256*fe 512*ff 256*fe 256*fd 256*fc 256*fb 256*fa 256*f9 256*f8 256*f7 256*f6 256*f5 256*f4 256*f3
  //   256*f2 256*f1 256*f0 256*ef 256*ee 256*ed 256*ec 256*eb 256*ea 256*e9 256*e8 256*e7 256*e6 256*e5
  //   256*e4 256*e3 256*e2 256*e1 256*e0 256*df 256*de 256*dd 256*dc 256*db 256*da 256*d9 256*d8 256*d7
  //   256*d6 256*d5 256*d4 256*d3 256*d2 256*d1 256*d0 256*cf 256*ce 256*cd 256*cc 256*cb 256*ca 256*c9
  //   256*c8 256*c7 256*c6 256*c5 256*c4 256*c3 256*c2 256*c1 256*c0 256*bf 256*be 256*bd 256*bc 256*bb
  //   256*ba 256*b9 256*b8 256*b7 256*b6 256*b5 256*b4 256*b3 256*b2 256*b1 256*b0 256*af 256*ae 256*ad
  //   256*ac 256*ab 256*aa 256*a9 256*a8 256*a7 256*a6 256*a5 256*a4 256*a3 256*a2 256*a1 256*a0 256*9f
  //   256*9e 256*9d 256*9c 256*9b 256*9a 256*99 256*98 256*97 256*96 256*95 256*94 256*93 256*92 256*91
  //   256*90 256*8f 256*8e 256*8d 256*8c 256*8b 256*8a 256*89 256*88 256*87 256*86 256*85 256*84 256*83
  //   256*82 256*81 256*80 256*7f 256*7e 256*7d 256*7c 256*7b 256*7a 256*79 256*78 256*77 256*76 256*75
  //   256*74 256*73 256*72 256*71 256*70 256*6f 256*6e 256*6d 256*6c 256*6b 256*6a 256*69 256*68 256*67
  //   256*66 256*65 256*64 256*63 256*62 256*61 256*60 256*5f 256*5e 256*5d 256*5c 256*5b 256*5a 256*59
  //   256*58 256*57 256*56 256*55 256*54 256*53 256*52 256*51 256*50 256*4f 256*4e 256*4d 256*4c 256*4b
  //   256*4a 256*49 256*48 256*47 256*46 256*45 256*44 256*43 256*42 256*41 256*40 256*3f 256*3e 256*3d
  //   256*3c 256*3b 256*3a 256*39 256*38 256*37 256*36 256*35 256*34 256*33 256*32 256*31 256*30 256*2f
  //   256*2e 256*2d 256*2c 256*2b 256*2a 256*29 256*28 256*27 256*26 256*25 256*24 256*23 256*22 256*21
  //   256*20 256*1f 256*1e 256*1d 256*1c 256*1b 256*1a 256*19 256*18 256*17 256*16 256*15 256*14 256*13
  //   256*12 256*11 256*10 256*f 256*e 256*d 256*c 256*b 256*a 256*9 256*8 256*7 256*6 256*5 256*4 256*3
  //   256*2 256*1 257*0 1 2 3 4 5 6 7 8 9 a b c d e f 10 11 12 13 14 15 16 17 18 19 1a 1b 1c 1d 1e 1f 20
  //   21 22 23 24 25 26 27 28 29 2a 2b 2c 2d 2e 2f 30 31 32 33 34 35 36 37 38 39 3a 3b 3c 3d 3e 3f 40 41
  //   42 43 44 45 46 47 48 49 4a 4b 4c 4d 4e 4f 50 51 52 53 54 55 56 57 58 59 5a 5b 5c 5d 5e 5f 60 61 62
  //   63 64 65 66 67 68 69 6a 6b 6c 6d 6e 6f 70 71 72 73 74 75 76 77 78 79 7a 7b 7c 7d 7e 7f 80 81 82 83
  //   84 85 86 87 88 89 8a 8b 8c 8d 8e 8f 90 91 92 93 94 95 96 97 98 99 9a 9b 9c 9d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
  //   contents of rom_3 (hex, n*v repeats v):
  //   256*0 256*1 256*2 256*3 256*4 256*5 256*6 256*7 256*8 256*9 256*a 256*b 256*c 256*d 256*e 256*f
  //   256*10 256*11 256*12 256*13 256*14 256*15 256*16 256*17 256*18 256*19 256*1a 256*1b 256*1c 256*1d
  //   256*1e 256*1f 256*20 256*21 256*22 256*23 256*24 256*25 256*26 256*27 256*28 256*29 256*2a 256*2b
  //   256*2c 256*2d 256*2e 256*2f 256*30 256*31 256*32 256*33 256*34 256*35 256*36 256*37 256*38 256*39
  //   256*3a 256*3b 256*3c 256*3d 256*3e 256*3f 256*40 256*41 256*42 256*43 256*44 256*45 256*46 256*47
  //   256*48 256*49 256*4a 256*4b 256*4c 256*4d 256*4e 256*4f 256*50 256*51 256*52 256*53 256*54 256*55
  //   256*56 256*57 256*58 256*59 256*5a 256*5b 256*5c 256*5d 256*5e 256*5f 256*60 256*61 256*62 256*63
  //   256*64 256*65 256*66 256*67 256*68 256*69 256*6a 256*6b 256*6c 256*6d 256*6e 256*6f 256*70 256*71
  //   256*72 256*73 256*74 256*75 256*76 256*77 256*78 256*79 256*7a 256*7b 256*7c 256*7d 256*7e 256*7f
  //   256*80 256*81 256*82 256*83 256*84 256*85 256*86 256*87 256*88 256*89 256*8a 256*8b 256*8c 256*8d
  //   256*8e 256*8f 256*90 256*91 256*92 256*93 256*94 256*95 256*96 256*97 256*98 256*99 256*9a 256*9b
  //   256*9c 256*9d 256*9e 256*9f 256*a0 256*a1 256*a2 256*a3 256*a4 256*a5 256*a6 256*a7 256*a8 256*a9
  //   256*aa 256*ab 256*ac 256*ad 256*ae 256*af 256*b0 256*b1 256*b2 256*b3 256*b4 256*b5 256*b6 256*b7
  //   256*b8 256*b9 256*ba 256*bb 256*bc 256*bd 256*be 256*bf 256*c0 256*c1 256*c2 256*c3 256*c4 256*c5
  //   256*c6 256*c7 256*c8 256*c9 256*ca 256*cb 256*cc 256*cd 256*ce 256*cf 256*d0 256*d1 256*d2 256*d3
  //   256*d4 256*d5 256*d6 256*d7 256*d8 256*d9 256*da 256*db 256*dc 256*dd 256*de 256*df 256*e0 256*e1
  //   256*e2 256*e3 256*e4 256*e5 256*e6 256*e7 256*e8 256*e9 256*ea 256*eb 256*ec 256*ed 256*ee 256*ef
  //   256*f0 256*f1 256*f2 256*f3 256*f4 256*f5 256*f6 256*f7 256*f8 256*f9 256*fa 256*fb 256*fc 256*fd
  //   256*fe 512*ff 256*fe 256*fd 256*fc 256*fb 256*fa 256*f9 256*f8 256*f7 256*f6 256*f5 256*f4 256*f3
  //   256*f2 256*f1 256*f0 256*ef 256*ee 256*ed 256*ec 256*eb 256*ea 256*e9 256*e8 256*e7 256*e6 256*e5
  //   256*e4 256*e3 256*e2 256*e1 256*e0 256*df 256*de 256*dd 256*dc 256*db 256*da 256*d9 256*d8 256*d7
  //   256*d6 256*d5 256*d4 256*d3 256*d2 256*d1 256*d0 256*cf 256*ce 256*cd 256*cc 256*cb 256*ca 256*c9
  //   256*c8 256*c7 256*c6 256*c5 256*c4 256*c3 256*c2 256*c1 256*c0 256*bf 256*be 256*bd 256*bc 256*bb
  //   256*ba 256*b9 256*b8 256*b7 256*b6 256*b5 256*b4 256*b3 256*b2 256*b1 256*b0 256*af 256*ae 256*ad
  //   256*ac 256*ab 256*aa 256*a9 256*a8 256*a7 256*a6 256*a5 256*a4 256*a3 256*a2 256*a1 256*a0 256*9f
  //   256*9e 256*9d 256*9c 256*9b 256*9a 256*99 256*98 256*97 256*96 256*95 256*94 256*93 256*92 256*91
  //   256*90 256*8f 256*8e 256*8d 256*8c 256*8b 256*8a 256*89 256*88 256*87 256*86 256*85 256*84 256*83
  //   256*82 256*81 256*80 256*7f 256*7e 256*7d 256*7c 256*7b 256*7a 256*79 256*78 256*77 256*76 256*75
  //   256*74 256*73 256*72 256*71 256*70 256*6f 256*6e 256*6d 256*6c 256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
  //   contents of controll_unit (hex, n*v repeats v):
  //   0 b800 a848 19c8 f008 b820 a8e8 15d8 f028 b840 b808 43d8 f048 b860 b808 4 0 b8c0 0 2 0 b8e0 0 0 f068
  //   b900 0 0 f0c8 0 0 0 f0e8 0 0 0 f108 0 0 0 e040 0 0 0 e0e0 0 0 0 51c8 0 0 0 d088 0 0 0 d0a8 0 0 0
  //   b128 0 0 0 b148 0 0 0 b168 0 0 0 b188 0 0 0 b1a8 0 0 0 35c8 0 0 0 63c8
endmodule

module BRB_COMPUTER (
);

  wire and_1_out, and_2_out, and_3_out, and_4_out, and_5_out, and_6_out, and_7_out, and_8_out, and_9_out,
       and_10_out, and_11_out, brb_cpu_1_inst_req, brb_cpu_1_int, brb_cpu_1_mem_r, brb_cpu_1_mem_w, BUTTONS,
       clk_out, clock_1_out, comparator_1_eq, CPU_SOFTWARE_INT, edge_detector2_1_q, KB, mmu_1_clk_out,
       mmu_1_d_grant, mmu_1_inst_grant, mmu_1_rom_grant, nand_1_out, not_1_out, not_2_out, or_1_out,
       or_2_out, or_3_out, pull_resistor_1_node, R, r_a, reg_file_1_e0, reg_file_1_e3, reg_file_1_e4,
       reg_file_1_e5, reg_file_1_e6, reg_file_1_e7, reg_file_2_e0, reg_file_2_e1, reg_file_2_e2,
       reg_file_2_e3, reg_file_2_e4, reg_file_2_e5, reg_file_2_e6, reg_file_2_e7, RESET_out, ROM_ACTIVE,
       ROM_APPROVED, rom_cpu_1_rom_req, ROM_DONE, ROM_OFF_WE, ROM_START_WE, s_r_l_1_q, SLEEP_out,
       smal_and_1_q, smal_and_2_q, smal_and_3_q, smal_and_4_q, smal_and_5_q, smal_and_6_q, smal_and_7_q,
       smal_and_8_q, smal_and_9_q, smal_and_10_q, smal_and_11_q, smal_and_12_q, smal_and_13_q, smal_and_14_q,
       smal_and_15_q, t_ff_1_q, undriven, undriven_2, undriven_3, undriven_4, undriven_5, undriven_6,
       undriven_7, undriven_8, undriven_9, undriven_10, undriven_11, undriven_12, W;
  wire [4:0] joystick_1_x, joystick_1_y;
  wire [5:0] button_1_out;
  wire [6:0] keyboard_1_data, reg_file_1_q0;
  wire [14:11] pull_resistor_5_node;
  wire [15:0] ADDR, BIOS_data, brb_cpu_1_inst_addr, brb_cpu_1_status, controlled_buffer_2_out, reg_file_1_q1,
       reg_file_1_q2, reg_file_1_q3, reg_file_1_q4, reg_file_1_q5, reg_file_1_q6, reg_file_1_q7,
       reg_file_2_q0, reg_file_2_q1, reg_file_2_q2, reg_file_2_q3, reg_file_2_q4, reg_file_2_q5,
       reg_file_2_q6, reg_file_2_q7, RET_ADDR_q, rom_1_data, rom_cpu_1_address, STAT_REG_q;
  wire [15:7] reg_file_1_q0_2;

  and and_1 (and_1_out, W, ROM_START_WE);
  and and_2 (and_2_out, W, ROM_OFF_WE);
  Pull_Resistor pull_resistor_1 (.node(pull_resistor_1_node));
  buf buffer_1 (pull_resistor_1_node, ROM_DONE);
  buf buffer_2 (pull_resistor_1_node, KB);
  buf buffer_3 (pull_resistor_1_node, BUTTONS);
  buf buffer_4 (pull_resistor_1_node, undriven);
  buf buffer_5 (pull_resistor_1_node, undriven_2);
  buf buffer_6 (pull_resistor_1_node, undriven_3);
  buf buffer_7 (pull_resistor_1_node, undriven_4);
  buf buffer_8 (pull_resistor_1_node, undriven_5);
  buf buffer_9 (pull_resistor_1_node, undriven_6);
  buf buffer_10 (pull_resistor_1_node, undriven_7);
  buf buffer_11 (pull_resistor_1_node, undriven_8);
  buf buffer_12 (pull_resistor_1_node, undriven_9);
  buf buffer_13 (pull_resistor_1_node, undriven_10);
  buf buffer_14 (pull_resistor_1_node, undriven_11);
  buf buffer_15 (pull_resistor_1_node, undriven_12);
  buf buffer_16 (pull_resistor_1_node, CPU_SOFTWARE_INT);
  ROM_CPU rom_cpu_1 (
    .START_WE(and_1_out), .TRANSFER_GRANT(mmu_1_rom_grant), .ADDR(controlled_buffer_2_out),
    .FINISH_WE(and_2_out), .CLK(mmu_1_clk_out), .WE_CLK(or_3_out), .DONE_ACCEPTED(ROM_APPROVED),
    .ADDRESS(rom_cpu_1_address), .DONE(ROM_DONE), .ROM_REQ(rom_cpu_1_rom_req), .active(r_a));
  not not_1 (not_1_out, or_3_out);
  or or_1 (or_1_out, brb_cpu_1_mem_w, brb_cpu_1_mem_r);
  edge_detector2 edge_detector2_1 (.HIGH(1'b1), .LOW(1'b0), .CLK(or_3_out), .Q(edge_detector2_1_q));
  S_R_L s_r_l_1 (.SET(RESET_out), .RESET(edge_detector2_1_q), .POR_RES(1'b0), .Q(s_r_l_1_q));
  Button RESET (.out(RESET_out));
  assign ADDR = mmu_1_rom_grant ? rom_cpu_1_address : 16'bz;  // Controlled_Buffer controlled_buffer_1
  Button SLEEP (.out(SLEEP_out));
  T_Flip_Flop t_ff_1 (.T(SLEEP_out), .clk(SLEEP_out), .Q(t_ff_1_q));  // open: Qn, reset, preset
  ROM #(.addrWidth(16), .dataWidth(16)) rom_1 (.addr(rom_cpu_1_address), .data(rom_1_data));
  MMU mmu_1 (
    .CPU_CLK(or_3_out), .ROM_CLK(or_3_out), .INST_CLK(not_1_out), .D_REQ(or_1_out),
    .ROM_REQ(rom_cpu_1_rom_req), .INST_REQ(brb_cpu_1_inst_req), .res(s_r_l_1_q), .CLK_OUT(mmu_1_clk_out),
    .D_GRANT(mmu_1_d_grant), .ROM_GRANT(mmu_1_rom_grant), .INST_GRANT(mmu_1_inst_grant));
  assign controlled_buffer_2_out = mmu_1_rom_grant ? rom_1_data : 16'bz;  // Controlled_Buffer controlled_buffer_2
  Pull_Resistor pull_resistor_2 (.node(ADDR));
  Pull_Resistor pull_resistor_3 (.node(controlled_buffer_2_out));
  // Probe on controlled_buffer_2_out
  MEM_ARBITER mem_arbiter_1 (
    .INST_GRANT(mmu_1_inst_grant), .D_GRANT(mmu_1_d_grant), .ROM_GRANT(mmu_1_rom_grant),
    .CPU_R(brb_cpu_1_mem_r), .CPU_W(brb_cpu_1_mem_w), .MEM_R(R), .MEM_W(W));
  brb_cpu brb_cpu_1 (
    .DATA_GRANT(mmu_1_d_grant), .D_IN(controlled_buffer_2_out), .INST_G(mmu_1_inst_grant), .clk(or_3_out),
    .res(s_r_l_1_q), .HALT(t_ff_1_q), .IRQ(pull_resistor_1_node), .INT(brb_cpu_1_int),
    .INST_ADDR(brb_cpu_1_inst_addr), .STATUS(brb_cpu_1_status), .INST_REQ(brb_cpu_1_inst_req),
    .D_Q(controlled_buffer_2_out), .ADDR(ADDR), .SOFT_INT(CPU_SOFTWARE_INT), .MEM_R(brb_cpu_1_mem_r),
    .MEM_W(brb_cpu_1_mem_w));
  and and_3 (and_3_out, ADDR[9], ADDR[10], ~ADDR[11]);  // AND_Gate
  and and_4 (and_4_out, ADDR[12], ADDR[13], ADDR[14], ADDR[15], 1'b1);
  Register #(.width(16)) RET_ADDR (
    .D(brb_cpu_1_inst_addr), .en(brb_cpu_1_int), .clk(brb_cpu_1_int), .Q(RET_ADDR_q), .clr(s_r_l_1_q));
  Register #(.width(16)) STAT_REG (
    .D(brb_cpu_1_status), .en(brb_cpu_1_int), .clk(brb_cpu_1_int), .Q(STAT_REG_q), .clr(s_r_l_1_q));
  or or_2 (or_2_out, and_3_out, ADDR[11]);
  nand nand_1 (nand_1_out, or_2_out, and_4_out);
  Comparator #(.mode("unsigned"), .width(16)) comparator_1 (
    .a(brb_cpu_1_inst_addr), .eq(comparator_1_eq));  // open: b, gt, lt
  and and_5 (and_5_out, ~ADDR[8], and_4_out, and_3_out);  // AND_Gate
  and and_6 (and_6_out, ADDR[11], and_4_out);
  Clock clock_1 (.out(clock_1_out));
  Pull_Resistor pull_resistor_4 (.node(comparator_1_eq));
  and and_7 (and_7_out, ~comparator_1_eq, clock_1_out);  // AND_Gate
  Button clk (.out(clk_out));
  or or_3 (or_3_out, and_7_out, clk_out);
  and and_8 (and_8_out, and_5_out, ADDR[4], ADDR[5], ADDR[6], ADDR[7]);
  ROM #(.dataWidth(16)) BIOS (.addr(ADDR[7:0]), .data(BIOS_data));
  RAM #(.addrWidth(16), .asyncread("true"), .dataWidth(16), .databus("bidir")) ram_1 (
    .addr(ADDR), .we(and_9_out), .oe(and_10_out), .clk(mmu_1_clk_out), .data(controlled_buffer_2_out));
  and and_9 (and_9_out, nand_1_out, W);
  and and_10 (and_10_out, nand_1_out, R);
  // RGB_Video #(.cursor("No Cursor"), .height(32), .scale(6), .width(64)) rgb_video_1: pin names not known; wires that end beside it: s_r_l_1_q, mmu_1_clk_out, and_6_out, controlled_buffer_2_out, controlled_buffer_2_out
  Keyboard keyboard_1 (.clk(mmu_1_clk_out), .re(smal_and_4_q), .clr(s_r_l_1_q), .avail(KB), .data(keyboard_1_data));
  assign controlled_buffer_2_out = and_11_out ? BIOS_data : 16'bz;  // Controlled_Buffer controlled_buffer_3
  and and_11 (and_11_out, ~ADDR[11], ADDR[10], ADDR[9], ADDR[8], R);  // AND_Gate
  Joystick #(.bits(5)) joystick_1 (.x(joystick_1_x), .y(joystick_1_y));
  Button button_1 (.out(button_1_out[0]));
  Button button_2 (.out(button_1_out[3]));
  Button button_3 (.out(button_1_out[1]));
  Button button_4 (.out(button_1_out[2]));
  Button ENT (.out(button_1_out[4]));
  Button DEL (.out(button_1_out[5]));
  Pull_Resistor pull_resistor_5 (.node({CPU_SOFTWARE_INT, pull_resistor_5_node, ROM_ACTIVE, ROM_DONE, BUTTONS, KB, keyboard_1_data}));
  TTY tty_1 (.data(reg_file_1_q0), .clk(mmu_1_clk_out), .we(reg_file_1_e0), .clr(reg_file_1_q0_2[7]));
  not not_2 (not_2_out, and_8_out);
  reg_file reg_file_1 (
    .NE(ADDR[3]), .E(and_8_out), .SEL(ADDR[2:0]), .D0(controlled_buffer_2_out), .D1(controlled_buffer_2_out),
    .D2(controlled_buffer_2_out), .D3({joystick_1_y, joystick_1_x, button_1_out}),
    .D4({CPU_SOFTWARE_INT, pull_resistor_5_node, ROM_ACTIVE, ROM_DONE, BUTTONS, KB, keyboard_1_data}),
    .D5(RET_ADDR_q), .D6(STAT_REG_q), .D7(controlled_buffer_2_out), .CLK(mmu_1_clk_out), .RES(s_r_l_1_q),
    .Q0({reg_file_1_q0_2[15:9], ROM_APPROVED, reg_file_1_q0_2[7], reg_file_1_q0}), .Q1(reg_file_1_q1),
    .Q2(reg_file_1_q2), .Q3(reg_file_1_q3), .Q4(reg_file_1_q4), .Q5(reg_file_1_q5), .Q6(reg_file_1_q6),
    .Q7(reg_file_1_q7), .E0(reg_file_1_e0), .E1(ROM_START_WE), .E2(ROM_OFF_WE), .E3(reg_file_1_e3),
    .E4(reg_file_1_e4), .E5(reg_file_1_e5), .E6(reg_file_1_e6), .E7(reg_file_1_e7));
  SMAL_AND smal_and_1 (.A(ROM_START_WE), .B(R), .Q(smal_and_1_q));
  SMAL_AND smal_and_2 (.A(ROM_OFF_WE), .B(R), .Q(smal_and_2_q));
  SMAL_AND smal_and_3 (.A(reg_file_1_e3), .B(R), .Q(smal_and_3_q));
  SMAL_AND smal_and_4 (.A(reg_file_1_e4), .B(R), .Q(smal_and_4_q));
  SMAL_AND smal_and_5 (.A(reg_file_1_e5), .B(R), .Q(smal_and_5_q));
  SMAL_AND smal_and_6 (.A(reg_file_1_e6), .B(R), .Q(smal_and_6_q));
  SMAL_AND smal_and_7 (.A(reg_file_1_e7), .B(R), .Q(smal_and_7_q));
  reg_file reg_file_2 (
    .NE(not_2_out), .E(ADDR[3]), .SEL(ADDR[2:0]), .D0(controlled_buffer_2_out), .D1(controlled_buffer_2_out),
    .D2(controlled_buffer_2_out), .D3(controlled_buffer_2_out), .D4(controlled_buffer_2_out),
    .D5(controlled_buffer_2_out), .D6(controlled_buffer_2_out), .D7(controlled_buffer_2_out),
    .CLK(mmu_1_clk_out), .RES(s_r_l_1_q), .Q0(reg_file_2_q0), .Q1(reg_file_2_q1), .Q2(reg_file_2_q2),
    .Q3(reg_file_2_q3), .Q4(reg_file_2_q4), .Q5(reg_file_2_q5), .Q6(reg_file_2_q6), .Q7(reg_file_2_q7),
    .E0(reg_file_2_e0), .E1(reg_file_2_e1), .E2(reg_file_2_e2), .E3(reg_file_2_e3), .E4(reg_file_2_e4),
    .E5(reg_file_2_e5), .E6(reg_file_2_e6), .E7(reg_file_2_e7));
  SMAL_AND smal_and_8 (.A(reg_file_2_e0), .B(R), .Q(smal_and_8_q));
  SMAL_AND smal_and_9 (.A(reg_file_2_e1), .B(R), .Q(smal_and_9_q));
  SMAL_AND smal_and_10 (.A(reg_file_2_e2), .B(R), .Q(smal_and_10_q));
  SMAL_AND smal_and_11 (.A(reg_file_2_e3), .B(R), .Q(smal_and_11_q));
  SMAL_AND smal_and_12 (.A(reg_file_2_e4), .B(R), .Q(smal_and_12_q));
  SMAL_AND smal_and_13 (.A(reg_file_2_e5), .B(R), .Q(smal_and_13_q));
  SMAL_AND smal_and_14 (.A(reg_file_2_e6), .B(R), .Q(smal_and_14_q));
  SMAL_AND smal_and_15 (.A(reg_file_2_e7), .Q(smal_and_15_q));  // open: B
  or or_4 (BUTTONS, 1'b0, reg_file_1_q3[0], reg_file_1_q3[1], reg_file_1_q3[2], reg_file_1_q3[3], reg_file_1_q3[4], reg_file_1_q3[5]);
  assign controlled_buffer_2_out = smal_and_1_q ? reg_file_1_q1 : 16'bz;  // Controlled_Buffer controlled_buffer_4
  assign controlled_buffer_2_out = smal_and_2_q ? reg_file_1_q2 : 16'bz;  // Controlled_Buffer controlled_buffer_5
  assign controlled_buffer_2_out = smal_and_3_q ? reg_file_1_q3 : 16'bz;  // Controlled_Buffer controlled_buffer_6
  assign controlled_buffer_2_out = smal_and_4_q ? reg_file_1_q4 : 16'bz;  // Controlled_Buffer controlled_buffer_7
  assign controlled_buffer_2_out = smal_and_5_q ? reg_file_1_q5 : 16'bz;  // Controlled_Buffer controlled_buffer_8
  assign controlled_buffer_2_out = smal_and_6_q ? reg_file_1_q6 : 16'bz;  // Controlled_Buffer controlled_buffer_9
  assign controlled_buffer_2_out = smal_and_7_q ? reg_file_1_q7 : 16'bz;  // Controlled_Buffer controlled_buffer_10
  assign controlled_buffer_2_out = smal_and_8_q ? reg_file_2_q0 : 16'bz;  // Controlled_Buffer controlled_buffer_11
  assign controlled_buffer_2_out = smal_and_9_q ? reg_file_2_q1 : 16'bz;  // Controlled_Buffer controlled_buffer_12
  assign controlled_buffer_2_out = smal_and_10_q ? reg_file_2_q2 : 16'bz;  // Controlled_Buffer controlled_buffer_13
  assign controlled_buffer_2_out = smal_and_11_q ? reg_file_2_q3 : 16'bz;  // Controlled_Buffer controlled_buffer_14
  assign controlled_buffer_2_out = smal_and_12_q ? reg_file_2_q4 : 16'bz;  // Controlled_Buffer controlled_buffer_15
  assign controlled_buffer_2_out = smal_and_13_q ? reg_file_2_q5 : 16'bz;  // Controlled_Buffer controlled_buffer_16
  assign controlled_buffer_2_out = smal_and_14_q ? reg_file_2_q6 : 16'bz;  // Controlled_Buffer controlled_buffer_17
  assign controlled_buffer_2_out = smal_and_15_q ? reg_file_2_q7 : 16'bz;  // Controlled_Buffer controlled_buffer_18

  // Notes on the sheet:
  //   buffer_1 drives only 1 and floats otherwise
  //   buffer_2 drives only 1 and floats otherwise
  //   buffer_3 drives only 1 and floats otherwise
  //   buffer_4 drives only 1 and floats otherwise
  //   buffer_5 drives only 1 and floats otherwise
  //   buffer_6 drives only 1 and floats otherwise
  //   buffer_7 drives only 1 and floats otherwise
  //   buffer_8 drives only 1 and floats otherwise
  //   buffer_9 drives only 1 and floats otherwise
  //   buffer_10 drives only 1 and floats otherwise
  //   buffer_11 drives only 1 and floats otherwise
  //   buffer_12 drives only 1 and floats otherwise
  //   buffer_13 drives only 1 and floats otherwise
  //   buffer_14 drives only 1 and floats otherwise
  //   buffer_15 drives only 1 and floats otherwise
  //   buffer_16 drives only 1 and floats otherwise
  //   contents of BIOS (hex, n*v repeats v):
  //   0 d003 f7d8 1003 80 2003 f6f0 200b 1 dd01 f d054 f7c2 f003 1 dd09 7f 3 f6f3 1007 20 1006 f722 f603 1
  //   9 f712 f603 80 3 f6f0 b f73e f003 80 3 f6f0 b f7e5 1003 1 dd01 f d054 f7c2 f003 1 dd09 a 1003 200
  //   2003 f6f0 100b 1 dd01 f d054 f768 f003 1 dd09 f5ff 3 f6f2 b 0 3 f6f1 b 0 1003 0 2003 0 3003 0 4003 0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
  //   F700-F7FF
  //   0000 - F5FF
  //   F800-FFFF
  //   F5FF - FFFF
  //   |
  //   V
  //   F6F0 - F6FF
endmodule

module ALU_8_bit (
  input  c_in,
  input  [7:0] b,
  input  [7:0] a,
  input  [3:0] M_OP,
  output [7:0] Q,
  output [3:0] FLAGS
);

  wire adder_1_cout, multiplexer_3_out, xor_1_out, xor_2_out;
  wire [1:0] c_op, sh_op;
  wire [2:0] rom_1_data;
  wire [7:0] b_t, multiplexer_1_out;
  wire [7:7] multiplexer_2_out;

  ROM #(.addrWidth(4), .dataWidth(7)) rom_1 (.addr(M_OP), .data({c_op, sh_op, rom_1_data}));
  ROM #(.addrWidth(19)) rom_2 (.addr({rom_1_data, b, a}), .data(b_t));
  Multiplexer #(.select(2), .width(8)) multiplexer_1 (
    .in0({8{1'b0}}), .in1({multiplexer_2_out[7], a[7:1]}), .in2({a[6:0], multiplexer_2_out[7]}), .in3(a),
    .out(multiplexer_1_out), .sel(sh_op));
  Multiplexer #(.select(2)) multiplexer_2 (
    .in0(c_in), .in1(1'b0), .in2(1'b1), .in3(a[7]), .out(multiplexer_2_out[7]));  // open: sel
  Multiplexer #(.select(2)) multiplexer_3 (
    .in0(multiplexer_2_out[7]), .in1(1'b0), .in2(1'b0), .in3(multiplexer_2_out[7]), .out(multiplexer_3_out));  // open: sel
  Adder adder_1 (
    .a(multiplexer_1_out), .b(b_t), .out({FLAGS[1], Q[6:0]}), .cin(multiplexer_3_out), .cout(adder_1_cout));
  Multiplexer #(.select(2)) multiplexer_4 (
    .in0(adder_1_cout), .in1(a[0]), .in2(a[7]), .in3(adder_1_cout), .out(FLAGS[2]));  // open: sel
  nor nor_1 (FLAGS[0], FLAGS[1], Q[6], Q[5], Q[4], Q[3], Q[2], Q[1], Q[0], 1'b0);
  xor xor_1 (xor_1_out, a[7], FLAGS[1]);
  xor xor_2 (xor_2_out, FLAGS[1], b_t[7]);
  and and_1 (FLAGS[3], xor_1_out, xor_2_out);

  assign Q[7] = FLAGS[1];

  // Notes on the sheet:
  //   contents of rom_1 (hex, n*v repeats v):
  //   38 18 59 19 21 41 22 23 24 28 8 30 10 68 20
  //   contents of rom_2 (hex, n*v repeats v):
  //   256*0 256*1 256*2 256*3 256*4 256*5 256*6 256*7 256*8 256*9 256*a 256*b 256*c 256*d 256*e 256*f
  //   256*10 256*11 256*12 256*13 256*14 256*15 256*16 256*17 256*18 256*19 256*1a 256*1b 256*1c 256*1d
  //   256*1e 256*1f 256*20 256*21 256*22 256*23 256*24 256*25 256*26 256*27 256*28 256*29 256*2a 256*2b
  //   256*2c 2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
endmodule
